// Logisim project 3.2.circ as structural Verilog: 3 circuits, main circuit cache_line
module main (
  input  [8:0] ADR,
  output [3:0] OTF,
  output [1:0] IND,
  output [2:0] TAG
);

  wire cache_1_hit, clock_1_out, clock_2_out, clock_3_out, comparator_1_eq, counter_1_carry, not_1_out,
       not_2_out;
  wire [4:0] register_1_q;
  wire [7:0] multiplexer_2_out;
  wire [63:0] cache_1_o, cache_2_o, multiplexer_1_out, ram_1_dout, ram_2_dout;

  Register #(.width(5)) register_1 (.D(ADR[8:4]), .Q(register_1_q), .clk(clock_1_out));  // open: en, clr
  not not_1 (not_1_out, comparator_1_eq);
  Counter #(.max('h3)) counter_1 (
    .load(not_1_out), .D(8'h1), .count(not_2_out), .carry(counter_1_carry), .clk(clock_1_out));  // open: Q, up, clr
  Clock clock_1 (.out(clock_1_out));
  Comparator #(.width(5)) comparator_1 (.a(ADR[8:4]), .b(register_1_q), .eq(comparator_1_eq));  // open: gt, lt
  Clock clock_2 (.out(clock_2_out));
  RAM #(.addrWidth(5), .asyncread("true"), .dataWidth(64)) ram_1 (
    .addr(ADR[8:4]), .oe(not_2_out), .clk(clock_2_out), .dout(ram_1_dout));  // open: we, din
  RAM #(.addrWidth(5), .asyncread("true"), .dataWidth(64)) ram_2 (
    .addr(ADR[8:4]), .oe(not_2_out), .clk(clock_2_out), .dout(ram_2_dout));  // open: we, din
  cache cache_1 (
    .IND(ADR[5:4]), .D(ram_1_dout), .TAG(ADR[8:6]), .CLK(counter_1_carry), .HIT(cache_1_hit), .O(cache_1_o));
  cache cache_2 (
    .IND(ADR[5:4]), .D(ram_2_dout), .TAG(ADR[8:6]), .CLK(counter_1_carry), .HIT(cache_1_hit), .O(cache_2_o));
  not not_2 (not_2_out, cache_1_hit);
  Multiplexer #(.width(64)) multiplexer_1 (.in0(cache_1_o), .in1(cache_2_o), .out(multiplexer_1_out), .sel(ADR[3]));
  Multiplexer #(.select(3), .width(8)) multiplexer_2 (
    .in0(multiplexer_1_out[7:0]), .in1(multiplexer_1_out[15:8]), .in2(multiplexer_1_out[23:16]),
    .in3(multiplexer_1_out[31:24]), .in4(multiplexer_1_out[39:32]), .in5(multiplexer_1_out[47:40]),
    .in6(multiplexer_1_out[55:48]), .in7(multiplexer_1_out[63:56]), .out(multiplexer_2_out), .sel(ADR[2:0]));
  Register register_2 (.D(multiplexer_2_out), .clk(clock_3_out), .clr(not_2_out));  // open: en, Q
  Clock clock_3 (.out(clock_3_out));

  assign IND = ADR[5:4];
  assign OTF = ADR[3:0];
  assign TAG = ADR[8:6];

  // Notes on the sheet:
  //   Длина строки: 16 слов (байт)
  //   Строк кэш-памяти: 4 строки
  //   Размер памяти: 512 байт
  //   Адрес: 3 бит тега + 2 бит индекса + 4 бит смещения
endmodule

module cache_line (
  input  [63:0] D,
  input  [2:0] TAG,
  input  CLK,
  input  WR,
  output [63:0] O,
  output HIT
);

  wire and_1_out, comparator_1_eq, register_6_q;
  wire [2:0] register_5_q;
  wire [15:0] register_1_q, register_2_q, register_3_q, register_4_q;

  and and_1 (and_1_out, WR, ~HIT);  // AND_Gate
  Register #(.width(16)) register_1 (.D(D[15:0]), .en(and_1_out), .Q(register_1_q), .clk(CLK));  // open: clr
  Register #(.width(16)) register_2 (.D(D[31:16]), .en(and_1_out), .Q(register_2_q), .clk(CLK));  // open: clr
  Register #(.width(16)) register_3 (.D(D[47:32]), .en(and_1_out), .Q(register_3_q), .clk(CLK));  // open: clr
  Register #(.width(16)) register_4 (.D(D[63:48]), .en(and_1_out), .Q(register_4_q), .clk(CLK));  // open: clr
  Register #(.width(3)) register_5 (.D(TAG), .en(and_1_out), .Q(register_5_q), .clk(CLK));  // open: clr
  Register #(.width(1)) register_6 (.D(and_1_out), .en(and_1_out), .Q(register_6_q), .clk(CLK));  // open: clr
  Comparator #(.width(3)) comparator_1 (.a(TAG), .b(register_5_q), .eq(comparator_1_eq));  // open: gt, lt
  Multiplexer #(.width(64)) multiplexer_1 (
    .in0({64{1'b0}}), .in1({register_4_q, register_3_q, register_2_q, register_1_q}), .out(O), .sel(HIT));
  and and_2 (HIT, comparator_1_eq, register_6_q);
endmodule

module cache (
  input  [1:0] IND,
  input  [63:0] D,
  input  [2:0] TAG,
  input  CLK,
  output HIT,
  output [63:0] O
);

  wire cache_line_1_hit, cache_line_2_hit, cache_line_3_hit, cache_line_4_hit, decoder_1_out0,
       decoder_1_out1, decoder_1_out2, decoder_1_out3;
  wire [63:0] cache_line_1_o, cache_line_2_o, cache_line_3_o, cache_line_4_o, multiplexer_2_out;

  Decoder #(.enable("false"), .select(2)) decoder_1 (
    .out0(decoder_1_out0), .out1(decoder_1_out1), .out2(decoder_1_out2), .out3(decoder_1_out3), .sel(IND));
  cache_line cache_line_1 (
    .D(D), .TAG(TAG), .CLK(CLK), .WR(decoder_1_out0), .O(cache_line_1_o), .HIT(cache_line_1_hit));
  cache_line cache_line_2 (
    .D(D), .TAG(TAG), .CLK(CLK), .WR(decoder_1_out1), .O(cache_line_2_o), .HIT(cache_line_2_hit));
  cache_line cache_line_3 (
    .D(D), .TAG(TAG), .CLK(CLK), .WR(decoder_1_out2), .O(cache_line_3_o), .HIT(cache_line_3_hit));
  cache_line cache_line_4 (
    .D(D), .TAG(TAG), .CLK(CLK), .WR(decoder_1_out3), .O(cache_line_4_o), .HIT(cache_line_4_hit));
  Multiplexer #(.select(2)) multiplexer_1 (
    .in0(cache_line_1_hit), .in1(cache_line_2_hit), .in2(cache_line_3_hit), .in3(cache_line_4_hit),
    .out(HIT), .sel(IND));
  Multiplexer #(.select(2), .width(64)) multiplexer_2 (
    .in0(cache_line_1_o), .in1(cache_line_2_o), .in2(cache_line_3_o), .in3(cache_line_4_o),
    .out(multiplexer_2_out), .sel(IND));
  Multiplexer #(.width(64)) multiplexer_3 (.in0(D), .in1(multiplexer_2_out), .out(O), .sel(HIT));
endmodule
