// Logisim project lab1.circ as structural Verilog: 1 circuit, main circuit main
module main (
  input  A,
  input  B,
  input  C,
  input  D,
  input  E,
  input  A2,
  input  B2,
  input  C2,
  input  D2,
  input  E2
);

  wire and_1_out, and_2_out, and_3_out, and_4_out, and_5_out, and_6_out, and_7_out, and_8_out, and_9_out,
       and_10_out, and_11_out, and_12_out, and_13_out, and_14_out, and_15_out, and_16_out, or_1_out,
       or_2_out, or_3_out, or_4_out, or_5_out, or_6_out, or_7_out, or_8_out, or_9_out, or_10_out, or_11_out,
       or_12_out, or_13_out, or_14_out;

  and and_1 (and_1_out, ~A, B, C, D, ~E);  // AND_Gate
  and and_2 (and_2_out, A, B, ~C, D, ~E);  // AND_Gate
  and and_3 (and_3_out, ~A, ~B, ~C, D, ~E);  // AND_Gate
  and and_4 (and_4_out, A, B, ~C, D, E);  // AND_Gate
  and and_5 (and_5_out, ~A, B, ~C, D, ~E);  // AND_Gate
  and and_6 (and_6_out, ~A, B, C, D, ~E);  // AND_Gate
  and and_7 (and_7_out, A, B, C, D, ~E);  // AND_Gate
  and and_8 (and_8_out, ~A, ~B, ~C, D, ~E);  // AND_Gate
  and and_9 (and_9_out, ~A, B, ~C, D, ~E);  // AND_Gate
  and and_10 (and_10_out, ~A, B, C, D, E);  // AND_Gate
  and and_11 (and_11_out, ~A, B, C, ~D, ~E);  // AND_Gate
  and and_12 (and_12_out, ~A, B, C, D, ~E);  // AND_Gate
  and and_13 (and_13_out, A, B, C, D, ~E);  // AND_Gate
  or or_1 (or_1_out, and_1_out, and_2_out, and_3_out, and_4_out, and_5_out);
  or or_2 (or_2_out, and_6_out, and_7_out, and_8_out, and_9_out, and_10_out);
  or or_3 (or_3_out, and_11_out, and_12_out, and_13_out);
  LED X (.in(or_1_out));
  LED Y (.in(or_2_out));
  LED Z (.in(or_3_out));
  or or_4 (or_4_out, A2, ~B2, ~C2, D2, E2);  // OR_Gate
  or or_5 (or_5_out, ~A2, ~B2, ~C2, ~D2, E2);  // OR_Gate
  or or_6 (or_6_out, A2, ~B2, ~C2, ~D2, ~E2);  // OR_Gate
  or or_7 (or_7_out, A2, ~B2, ~C2, D2, E2);  // OR_Gate
  or or_8 (or_8_out, ~A2, ~B2, C2, ~D2, E2);  // OR_Gate
  or or_9 (or_9_out, ~A2, ~B2, C2, ~D2, ~E2);  // OR_Gate
  or or_10 (or_10_out, ~A2, ~B2, C2, ~D2, E2);  // OR_Gate
  or or_11 (or_11_out, A2, B2, C2, ~D2, E2);  // OR_Gate
  or or_12 (or_12_out, ~A2, ~B2, C2, ~D2, ~E2);  // OR_Gate
  or or_13 (or_13_out, A2, ~B2, C2, ~D2, E2);  // OR_Gate
  or or_14 (or_14_out, A2, ~B2, ~C2, ~D2, ~E2);  // OR_Gate
  and and_14 (and_14_out, or_4_out, or_5_out, or_6_out);
  LED X2 (.in(and_14_out));
  and and_15 (and_15_out, or_7_out, or_8_out, or_9_out);
  LED Y2 (.in(and_15_out));
  and and_16 (and_16_out, or_10_out, or_11_out, or_12_out, or_13_out, or_14_out);
  LED Z2 (.in(and_16_out));

  // Notes on the sheet:
  //   СДНФ
  //   СКНФ
endmodule
