// Logisim project lab2.circ as structural Verilog: 2 circuits, main circuit R
module main (
  input  writing,
  input  [7:0] adr,
  input  [23:0] in_3,
  output [6:0] RR
);

  wire clock_1_out;
  wire [2:0] bit_extender_5_out;
  wire [6:0] bit_extender_1_out, bit_extender_2_out, bit_extender_3_out, bit_extender_4_out,
       demultiplexer_1_out0, demultiplexer_1_out1, demultiplexer_2_out0, demultiplexer_3_out0,
       demultiplexer_4_out0;
  wire [7:0] divider_1_rem;

  assign bit_extender_1_out = {{1{1'b0}}, in_3[5:0]};  // Bit_Extender bit_extender_1
  assign bit_extender_2_out = {{1{1'b0}}, in_3[11:6]};  // Bit_Extender bit_extender_2
  assign bit_extender_3_out = {{1{1'b0}}, in_3[17:12]};  // Bit_Extender bit_extender_3
  assign bit_extender_4_out = {{1{1'b0}}, in_3[23:18]};  // Bit_Extender bit_extender_4
  R r_1 (.M4(in_3[5:0]), .M3(in_3[11:6]), .M2(in_3[17:12]), .M1(in_3[23:18]), .Rr(RR));
  Bit_Extender #(.out_width(3), .\type ("zero")) bit_extender_5 (.in(divider_1_rem), .out(bit_extender_5_out));
  Divider divider_1 (.a(adr), .b(8'h5), .rem(divider_1_rem));  // open: out, upper
  Demultiplexer #(.select(3), .tristate("true"), .width(7)) demultiplexer_1 (
    .out0(demultiplexer_1_out0), .out1(demultiplexer_1_out1), .out2(demultiplexer_1_out1),
    .out3(demultiplexer_1_out1), .out4(demultiplexer_1_out1), .in(bit_extender_1_out),
    .sel(bit_extender_5_out));  // open: out5, out6, out7
  Demultiplexer #(.select(3), .tristate("true"), .width(7)) demultiplexer_2 (
    .out0(demultiplexer_2_out0), .out1(demultiplexer_2_out0), .out2(demultiplexer_1_out0),
    .out3(demultiplexer_1_out0), .out4(demultiplexer_1_out0), .in(bit_extender_2_out),
    .sel(bit_extender_5_out));  // open: out5, out6, out7
  Demultiplexer #(.select(3), .tristate("true"), .width(7)) demultiplexer_3 (
    .out0(demultiplexer_3_out0), .out1(demultiplexer_3_out0), .out2(demultiplexer_3_out0),
    .out3(demultiplexer_2_out0), .out4(demultiplexer_2_out0), .in(bit_extender_3_out),
    .sel(bit_extender_5_out));  // open: out5, out6, out7
  Demultiplexer #(.select(3), .tristate("true"), .width(7)) demultiplexer_4 (
    .out0(demultiplexer_4_out0), .out1(demultiplexer_4_out0), .out2(demultiplexer_4_out0),
    .out3(demultiplexer_4_out0), .out4(demultiplexer_3_out0), .in(bit_extender_4_out),
    .sel(bit_extender_5_out));  // open: out5, out6, out7
  Demultiplexer #(.select(3), .tristate("true"), .width(7)) demultiplexer_5 (
    .out0(demultiplexer_1_out1), .out1(demultiplexer_1_out0), .out2(demultiplexer_2_out0),
    .out3(demultiplexer_3_out0), .out4(demultiplexer_4_out0), .in(RR), .sel(bit_extender_5_out));  // open: out5, out6, out7
  Clock clock_1 (.out(clock_1_out));
  RAM #(.dataWidth(7)) ram_1 (
    .addr(adr), .we(writing), .clk(clock_1_out), .din(demultiplexer_4_out0));  // open: oe, dout
  RAM #(.dataWidth(7)) ram_2 (
    .addr(adr), .we(writing), .clk(clock_1_out), .din(demultiplexer_3_out0));  // open: oe, dout
  RAM #(.dataWidth(7)) ram_3 (
    .addr(adr), .we(writing), .clk(clock_1_out), .din(demultiplexer_2_out0));  // open: oe, dout
  RAM #(.dataWidth(7)) ram_4 (
    .addr(adr), .we(writing), .clk(clock_1_out), .din(demultiplexer_1_out0));  // open: oe, dout
  RAM #(.dataWidth(7)) ram_5 (
    .addr(adr), .we(writing), .clk(clock_1_out), .din(demultiplexer_1_out1));  // open: oe, dout
endmodule

module R (
  input  [5:0] M4,
  input  [5:0] M3,
  input  [5:0] M2,
  input  [5:0] M1,
  output [6:0] Rr
);

  wire [5:0] adder_1_out, adder_2_out;
  wire [6:6] adder_1_cout, adder_2_cout;

  Adder #(.width(6)) adder_1 (.a(M4), .b(M3), .out(adder_1_out), .cout(adder_1_cout[6]));  // open: cin
  Adder #(.width(6)) adder_2 (.a(M2), .b(M1), .out(adder_2_out), .cout(adder_2_cout[6]));  // open: cin
  assign Rr = {adder_1_cout[6], adder_1_out} ^ {adder_2_cout[6], adder_2_out};  // XOR_Gate xor_1, 7 bits wide
endmodule
