// Logisim project 1.Martynenko_automata.circ as structural Verilog: 5 circuits, main circuit main
module main (
  input  [7:0] in_1,
  input  [6:0] in_2,
  output [3:0] out_3,
  output x1,
  output x2,
  output [3:0] out_6,
  output [3:0] out_7,
  output [3:0] out_8,
  output [3:0] out_9,
  output [3:0] out_10,
  output [3:0] out_11
);

  wire a, and_1_out, and_2_out, and_3_out, and_4_out, and_5_out, and_6_out, and_7_out, and_8_out, and_9_out,
       and_11_out, and_12_out, and_13_out, and_14_out, and_15_out, and_16_out, and_17_out, and_18_out,
       and_19_out, and_20_out, and_21_out, and_24_out, and_25_out, and_26_out, b, buzzer_1_p3, c_out, clear,
       clear_b, clk, comparator_2_eq, comparator_8_lt, counter_1_carry, counter_2_carry, counter_3_carry,
       counter_4_carry, counter_5_carry, counter_7_carry, counter_9_carry, d, d_ff_1_q, d_ff_1_qn, d_ff_2_q,
       d_ff_2_qn, d_ff_3_qn, d_ff_4_qn, due, f0, f1, f2, f3, f4, f5, f6, i1, i2, i3, i4, ic_1_f0, ic_1_f1,
       ic_1_f2, ic_1_f3, ic_1_f4, ic_1_f5, ic_1_f6, ic_2_f0, ic_2_f1, ic_2_f2, ic_2_f3, ic_2_f4, ic_2_f5,
       ic_2_f6, ic_3_f0, ic_3_f1, ic_3_f2, ic_3_f3, ic_3_f4, ic_3_f5, ic_3_f6, ic_4_f0, ic_4_f1, ic_4_f2,
       ic_4_f3, ic_4_f4, ic_4_f5, ic_4_f6, ic_5_f0, ic_5_f1, ic_5_f2, ic_5_f3, ic_5_f4, ic_5_f5, ic_5_f6,
       isA, isH, isM, isWork, L1, L2, L3, L4, L5, L6, L7, L8, L9, L81, m0, m1, m2, m3, m4, m5, m6, min,
       music_1_m0, music_1_m1, music_1_m2, music_1_m3, music_1_m4, music_1_m5, music_1_m6, nor_1_out,
       nor_2_out, not_1_out, not_2_out, not_3_out, not_4_out, not_5_out, not_6_out, not_7_out, or_4_out,
       or_5_out, or_6_out, or_7_out, or_8_out, or_9_out, or_10_out, press, tact, tt, up, up_b;
  wire [2:0] counter_2_q, counter_6_q, counter_7_q, counter_8_q, counter_10_q;
  wire [3:0] am, bit_extender_2_out, bit_extender_3_out, bit_extender_4_out, bit_extender_5_out,
       controlled_buffer_31_out, controlled_buffer_32_out, controlled_buffer_33_out, h, h2, h_dec, h_dec_b,
       h_ed, h_ed2, h_ed2_b, h_ed_b, m_b, m_ed2, min_dec, min_dec_b, min_dec_t, min_ed, min_ed_b, min_ed_t,
       multiplexer_1_out, multiplexer_2_out, multiplexer_3_out, multiplexer_4_out, multiplexer_5_out,
       multiplexer_6_out, multiplexer_7_out, multiplier_1_out, multiplier_2_out, multiplier_3_out,
       multiplier_4_out, multiplier_5_out, sec_dec, sec_dec_c, sec_ed, sec_ed_c, undriven, undriven_2,
       undriven_3, undriven_4, undriven_5;
  wire [13:0] freq;

  or or_1 (press, a, b, c_out, d);
  _7_Segment_Display u_7_segment_display_1 (.g(f0), .f(f1), .a(f2), .b(f3), .e(f6), .d(f5), .c(f4));  // open: dp
  or or_2 (x1, d, c_out);
  Button u_a (.out(a));
  Hex_Digit_Display hex_digit_display_1 (.value(multiplexer_1_out));  // open: dp
  Hex_Digit_Display hex_digit_display_2 (.value(multiplexer_2_out));  // open: dp
  Multiplexer #(.width(4)) multiplexer_1 (.in0(h_dec), .in1(h_dec_b), .out(multiplexer_1_out), .sel(L6));
  Multiplexer #(.width(4)) multiplexer_2 (.in0(h_ed), .in1(h_ed_b), .out(multiplexer_2_out), .sel(L6));
  or or_3 (x2, d, b);
  Button c (.out(c_out));
  Button u_b (.out(b));
  Button u_d (.out(d));
  Hex_Digit_Display hex_digit_display_3 (.value(multiplexer_3_out));  // open: dp
  Multiplexer #(.width(4)) multiplexer_3 (.in0(multiplexer_4_out), .in1(min_dec_t), .out(multiplexer_3_out), .sel(L3));
  Multiplexer #(.width(4)) multiplexer_4 (.in0(min_dec), .in1(min_dec_b), .out(multiplexer_4_out), .sel(L6));
  Clock clock_1 (.out(clk));
  and and_1 (and_1_out, clk, not_1_out);
  not not_1 (not_1_out, L9);
  Hex_Digit_Display hex_digit_display_4 (.value(multiplexer_5_out));  // open: dp
  Multiplexer #(.width(4)) multiplexer_5 (.in0(multiplexer_6_out), .in1(min_ed_t), .out(multiplexer_5_out), .sel(L3));
  Multiplexer #(.width(4)) multiplexer_6 (.in0(min_ed), .in1(min_ed_b), .out(multiplexer_6_out), .sel(L6));
  Counter #(.max('h9), .trigger("falling"), .width(4)) counter_1 (
    .clk(and_1_out), .D(undriven), .carry(counter_1_carry), .Q(sec_ed_c));  // open: clr, load, up, count
  Hex_Digit_Display hex_digit_display_5 (.value(sec_dec));  // open: dp
  Hex_Digit_Display hex_digit_display_6 (.value(sec_ed));  // open: dp
  _7_Segment_Display u_7_segment_display_2 (.g(m0), .f(m1), .a(m2), .b(m3), .e(m6), .d(m5), .c(m4));  // open: dp
  LED led_1 (.in(isWork));
  // Buzzer buzzer_1: pin names not known; wires that end beside it: in_1, freq, buzzer_1_p3, in_2
  assign buzzer_1_p3 = and_2_out ? or_4_out : 1'bz;  // Controlled_Buffer controlled_buffer_1
  Multiplier #(.width(4)) multiplier_1 (.a(sec_dec_c), .b(4'b1010), .out(multiplier_1_out));  // open: cin, cout
  Counter #(.max('h5), .trigger("falling"), .width(3)) counter_2 (
    .clk(counter_1_carry), .carry(counter_2_carry), .Q(counter_2_q));  // open: clr, load, up, count, D
  and and_2 (and_2_out, L1, L2);
  or or_4 (or_4_out, up, up_b);
  Register #(.trigger("falling"), .width(4)) register_1 (.D(out_6), .clk(press), .Q(out_7));  // open: en, clr
  Adder #(.width(4)) adder_1 (.a(sec_ed_c), .b(multiplier_1_out), .out(out_8));  // open: cin, cout
  assign sec_dec_c = {{1{1'b0}}, counter_2_q};  // Bit_Extender bit_extender_1
  not not_2 (not_2_out, L6);
  Counter #(.max('h9), .trigger("falling"), .width(4)) counter_3 (
    .clr(min), .clk(or_5_out), .D(undriven_2), .carry(counter_3_carry), .Q(m_ed2));  // open: load, up, count
  and and_3 (and_3_out, not_2_out, b, i1);
  or or_5 (or_5_out, and_3_out, counter_2_carry);
  and and_4 (and_4_out, i2, a, L6);
  Counter #(.max('h9), .trigger("falling"), .width(4)) counter_4 (
    .clr(counter_7_carry), .clk(and_5_out), .D(undriven_3), .carry(counter_4_carry), .Q(m_b));  // open: load, up, count
  and and_5 (and_5_out, i1, a, L6);
  and and_6 (and_6_out, L2, not_3_out);
  assign min_ed = and_6_out ? m_ed2 : 4'bz;  // Controlled_Buffer controlled_buffer_2
  and and_7 (and_7_out, L1, L2);
  FiL fil_1 (
    .x1(x1), .x2(x2), .q1(out_7[3]), .q2(out_7[2]), .q3(out_7[1]), .q4(out_7[0]), .i1(i1), .L1(L1),
    .EQ1(out_6[3]), .i3(i3), .L2(L2), .EQ4(out_6[0]), .EQ3(out_6[1]), .L3(L3), .i4(i4), .L4(L4), .L5(L5),
    .EQ2(out_6[2]), .L6(L6), .i2(i2), .L7(L7), .L8(L81));  // open: L9
  Counter #(.max('h9), .width(4)) counter_5 (
    .clr(clear_b), .clk(and_4_out), .D(undriven_4), .carry(counter_5_carry), .Q(h_ed2_b));  // open: load, up, count
  not not_3 (not_3_out, L3);
  S_R_Flip_Flop #(.trigger("falling")) s_r_ff_1 (.S(i1), .Q(L9), .reset(and_7_out), .preset(i1));  // open: R, clk, Qn
  D_Flip_Flop #(.trigger("falling")) d_ff_1 (
    .D(d_ff_1_qn), .clk(and_8_out), .Q(d_ff_1_q), .Qn(d_ff_1_qn));  // open: preset, reset
  and and_8 (and_8_out, i4, d, L6);
  Counter #(.max('h6), .trigger("falling"), .width(3)) counter_6 (
    .clr(min), .clk(counter_3_carry), .carry(min), .Q(counter_6_q));  // open: load, up, count, D
  Multiplexer #(.width(4)) multiplexer_7 (.in0(4'b1010), .in1(4'b1011), .out(multiplexer_7_out), .sel(d_ff_1_q));
  and and_9 (and_9_out, L2, L6);
  assign min_ed_b = and_9_out ? m_b : 4'bz;  // Controlled_Buffer controlled_buffer_3
  and and_10 (L8, L81, a);
  and and_11 (and_11_out, L1, L6);
  assign h_ed_b = and_11_out ? h_ed2_b : 4'bz;  // Controlled_Buffer controlled_buffer_4
  Counter #(.max('h6), .trigger("falling"), .width(3)) counter_7 (
    .clr(counter_7_carry), .clk(counter_4_carry), .carry(counter_7_carry), .Q(counter_7_q));  // open: load, up, count, D
  Multiplier #(.width(4)) multiplier_2 (.a(min_dec), .b(4'b1010), .out(multiplier_2_out));  // open: cin, cout
  not not_4 (not_4_out, L6);
  Comparator #(.width(4)) comparator_1 (.a(am), .b(multiplexer_7_out), .eq(isA));  // open: gt, lt
  Counter #(.max('h2), .trigger("falling"), .width(3)) counter_8 (
    .clr(clear_b), .clk(counter_5_carry), .Q(counter_8_q));  // open: load, up, count, D, carry
  Adder #(.width(4)) adder_2 (.a(m_ed2), .b(multiplier_2_out), .out(out_3));  // open: cin, cout
  Counter #(.max('h9), .trigger("falling"), .width(4)) counter_9 (
    .clr(clear), .clk(or_6_out), .D(undriven_5), .carry(counter_9_carry), .Q(h_ed2));  // open: load, up, count
  and and_12 (and_12_out, not_4_out, b, i2);
  or or_6 (or_6_out, and_12_out, min);
  assign bit_extender_2_out = {{1{1'b0}}, counter_6_q};  // Bit_Extender bit_extender_2
  assign min_dec = L2 ? bit_extender_2_out : 4'bz;  // Controlled_Buffer controlled_buffer_5
  Comparator #(.width(4)) comparator_2 (.a(h), .b(4'b1011), .eq(comparator_2_eq));  // open: gt, lt
  and and_13 (and_13_out, comparator_2_eq, min);
  and and_14 (and_14_out, i4, a);
  assign bit_extender_3_out = {{1{1'b0}}, counter_7_q};  // Bit_Extender bit_extender_3
  D_Flip_Flop #(.trigger("falling")) d_ff_2 (
    .D(d_ff_2_qn), .clk(or_7_out), .Q(d_ff_2_q), .Qn(d_ff_2_qn));  // open: preset, reset
  or or_7 (or_7_out, and_13_out, and_14_out);
  ic ic_1 (
    .simbols(multiplexer_7_out), .f6(ic_1_f6), .f5(ic_1_f5), .f4(ic_1_f4), .f0(ic_1_f0), .f1(ic_1_f1),
    .f2(ic_1_f2), .f3(ic_1_f3));  // open: out_2
  assign f6 = and_16_out ? ic_1_f6 : 1'bz;  // Controlled_Buffer controlled_buffer_6
  assign bit_extender_4_out = {{1{1'b0}}, counter_8_q};  // Bit_Extender bit_extender_4
  assign h_dec_b = and_17_out ? bit_extender_4_out : 4'bz;  // Controlled_Buffer controlled_buffer_7
  and and_15 (and_15_out, L2, L6);
  assign min_dec_b = and_15_out ? bit_extender_3_out : 4'bz;  // Controlled_Buffer controlled_buffer_8
  assign h_ed = L1 ? h_ed2 : 4'bz;  // Controlled_Buffer controlled_buffer_9
  Multiplexer #(.width(4)) multiplexer_8 (.in0(4'b1010), .in1(4'b1011), .out(am), .sel(d_ff_2_q));
  and and_16 (and_16_out, L6, L1);
  assign f5 = and_16_out ? ic_1_f5 : 1'bz;  // Controlled_Buffer controlled_buffer_10
  Multiplier #(.width(4)) multiplier_3 (
    .a(bit_extender_4_out), .b(4'b1010), .out(multiplier_3_out));  // open: cin, cout
  and and_17 (and_17_out, L1, L6);
  Adder #(.width(4)) adder_3 (.a(m_b), .b(multiplier_4_out), .out(out_11));  // open: cin, cout
  Multiplier #(.width(4)) multiplier_4 (
    .a(bit_extender_3_out), .b(4'b1010), .out(multiplier_4_out));  // open: cin, cout
  assign f4 = and_16_out ? ic_1_f4 : 1'bz;  // Controlled_Buffer controlled_buffer_11
  assign f0 = and_16_out ? ic_1_f0 : 1'bz;  // Controlled_Buffer controlled_buffer_12
  Comparator #(.width(4)) comparator_3 (.a(h), .b(h2), .eq(isH));  // open: gt, lt
  Adder #(.width(4)) adder_4 (.a(h_ed2_b), .b(multiplier_3_out), .out(h2));  // open: cin, cout
  Counter #(.max('h2), .trigger("falling"), .width(3)) counter_10 (
    .clr(clear), .clk(counter_9_carry), .Q(counter_10_q));  // open: load, up, count, D, carry
  assign f1 = and_16_out ? ic_1_f1 : 1'bz;  // Controlled_Buffer controlled_buffer_13
  Comparator #(.width(4)) comparator_4 (.a(4'b1100), .b(h2), .eq(clear_b));  // open: gt, lt
  Comparator #(.width(4)) comparator_5 (.a(out_3), .b(out_11), .eq(isM));  // open: gt, lt
  assign f2 = and_16_out ? ic_1_f2 : 1'bz;  // Controlled_Buffer controlled_buffer_14
  ic ic_2 (
    .simbols(am), .f6(ic_2_f6), .f5(ic_2_f5), .f4(ic_2_f4), .f0(ic_2_f0), .f1(ic_2_f1), .f2(ic_2_f2),
    .f3(ic_2_f3));  // open: out_2
  assign f6 = and_18_out ? ic_2_f6 : 1'bz;  // Controlled_Buffer controlled_buffer_15
  music music_1 (
    .min_ed(min_ed), .min_dec(min_dec), .L8(L8), .freq(freq), .up(up), .m6(music_1_m6), .m5(music_1_m5),
    .m4(music_1_m4), .m0(music_1_m0), .m1(music_1_m1), .m2(music_1_m2), .m3(music_1_m3));
  assign m3 = L81 ? music_1_m3 : 1'bz;  // Controlled_Buffer controlled_buffer_16
  stopwatch stopwatch_1 (
    .i3(i3), .clk(clk), .L3(L3), .a(a), .L5(L5), .sec_ed(sec_ed), .min_ed_t(min_ed_t), .sec_dec(sec_dec),
    .min_dec_t(min_dec_t));
  assign f3 = and_16_out ? ic_1_f3 : 1'bz;  // Controlled_Buffer controlled_buffer_17
  assign bit_extender_5_out = {{1{1'b0}}, counter_10_q};  // Bit_Extender bit_extender_5
  assign h_dec = L1 ? bit_extender_5_out : 4'bz;  // Controlled_Buffer controlled_buffer_18
  and and_18 (and_18_out, L1, not_5_out);
  assign f5 = and_18_out ? ic_2_f5 : 1'bz;  // Controlled_Buffer controlled_buffer_19
  assign m2 = L81 ? music_1_m2 : 1'bz;  // Controlled_Buffer controlled_buffer_20
  Multiplier #(.width(4)) multiplier_5 (
    .a(bit_extender_5_out), .b(4'b1010), .out(multiplier_5_out));  // open: cin, cout
  not not_5 (not_5_out, L6);
  assign f4 = and_18_out ? ic_2_f4 : 1'bz;  // Controlled_Buffer controlled_buffer_21
  assign f0 = and_18_out ? ic_2_f0 : 1'bz;  // Controlled_Buffer controlled_buffer_22
  assign m0 = L81 ? music_1_m0 : 1'bz;  // Controlled_Buffer controlled_buffer_23
  assign m1 = L81 ? music_1_m1 : 1'bz;  // Controlled_Buffer controlled_buffer_24
  and and_19 (and_19_out, isH, isM, isA);
  and and_20 (and_20_out, L7, b);
  Adder #(.width(4)) adder_5 (.a(h_ed2), .b(multiplier_5_out), .out(h));  // open: cin, cout
  assign f1 = and_18_out ? ic_2_f1 : 1'bz;  // Controlled_Buffer controlled_buffer_25
  assign m4 = L81 ? music_1_m4 : 1'bz;  // Controlled_Buffer controlled_buffer_26
  Adder #(.width(4)) adder_6 (.a(4'b1010), .b(4'b0000), .out(out_9));  // open: cin, cout
  and and_21 (and_21_out, isH, isA, isM, isWork, due);
  D_Flip_Flop d_ff_3 (.D(d_ff_3_qn), .clk(and_20_out), .Q(isWork), .Qn(d_ff_3_qn));  // open: preset, reset
  Comparator #(.width(4)) comparator_6 (.a(4'b1100), .b(h), .eq(clear));  // open: gt, lt
  assign f2 = and_18_out ? ic_2_f2 : 1'bz;  // Controlled_Buffer controlled_buffer_27
  assign m5 = L81 ? music_1_m5 : 1'bz;  // Controlled_Buffer controlled_buffer_28
  Comparator #(.width(4)) comparator_7 (.a(4'b0000), .b(out_8), .eq(tact));  // open: gt, lt
  Comparator #(.width(4)) comparator_8 (.a(out_9), .b(out_8), .lt(comparator_8_lt));  // open: gt, eq
  and and_22 (up_b, and_21_out, not_6_out);
  not not_6 (not_6_out, tt);
  assign f3 = and_18_out ? ic_2_f3 : 1'bz;  // Controlled_Buffer controlled_buffer_29
  assign m6 = L81 ? music_1_m6 : 1'bz;  // Controlled_Buffer controlled_buffer_30
  and and_23 (due, comparator_8_lt, and_19_out);
  D_Flip_Flop #(.trigger("falling")) d_ff_4 (
    .D(d_ff_4_qn), .clk(up_b), .Q(tt), .Qn(d_ff_4_qn), .reset(not_7_out));  // open: preset
  or or_8 (or_8_out, L1, L2);
  not not_7 (not_7_out, isM);
  and and_24 (and_24_out, or_8_out, nor_1_out);
  nor nor_1 (nor_1_out, L3, L4, L5, L6, L7);
  or or_9 (or_9_out, L3, L4, L5);
  nor nor_2 (nor_2_out, L1, L6, L7);
  or or_10 (or_10_out, L6, L7);
  assign controlled_buffer_31_out = and_24_out ? 4'b1101 : 4'bz;  // Controlled_Buffer controlled_buffer_31
  assign controlled_buffer_32_out = and_25_out ? 4'b0101 : 4'bz;  // Controlled_Buffer controlled_buffer_32
  and and_25 (and_25_out, or_9_out, nor_2_out);
  assign controlled_buffer_33_out = and_26_out ? 4'b1100 : 4'bz;  // Controlled_Buffer controlled_buffer_33
  buf and_26 (and_26_out, or_10_out);  // AND_Gate
  ic ic_3 (
    .simbols(controlled_buffer_31_out), .f6(ic_3_f6), .f5(ic_3_f5), .f4(ic_3_f4), .f0(ic_3_f0), .f1(ic_3_f1),
    .f2(ic_3_f2), .f3(ic_3_f3));  // open: out_2
  assign m2 = and_24_out ? ic_3_f2 : 1'bz;  // Controlled_Buffer controlled_buffer_34
  assign m3 = and_24_out ? ic_3_f3 : 1'bz;  // Controlled_Buffer controlled_buffer_35
  ic ic_4 (
    .simbols(controlled_buffer_32_out), .f6(ic_4_f6), .f5(ic_4_f5), .f4(ic_4_f4), .f0(ic_4_f0), .f1(ic_4_f1),
    .f2(ic_4_f2), .f3(ic_4_f3));  // open: out_2
  assign m3 = and_25_out ? ic_4_f3 : 1'bz;  // Controlled_Buffer controlled_buffer_36
  ic ic_5 (
    .simbols(controlled_buffer_33_out), .f6(ic_5_f6), .f5(ic_5_f5), .f4(ic_5_f4), .f0(ic_5_f0), .f1(ic_5_f1),
    .f2(ic_5_f2), .f3(ic_5_f3));  // open: out_2
  assign m3 = and_26_out ? ic_5_f3 : 1'bz;  // Controlled_Buffer controlled_buffer_37
  assign m1 = and_24_out ? ic_3_f1 : 1'bz;  // Controlled_Buffer controlled_buffer_38
  assign m2 = and_25_out ? ic_4_f2 : 1'bz;  // Controlled_Buffer controlled_buffer_39
  assign m2 = and_26_out ? ic_5_f2 : 1'bz;  // Controlled_Buffer controlled_buffer_40
  assign m0 = and_24_out ? ic_3_f0 : 1'bz;  // Controlled_Buffer controlled_buffer_41
  assign m0 = and_25_out ? ic_4_f0 : 1'bz;  // Controlled_Buffer controlled_buffer_42
  assign m1 = and_25_out ? ic_4_f1 : 1'bz;  // Controlled_Buffer controlled_buffer_43
  assign m1 = and_26_out ? ic_5_f1 : 1'bz;  // Controlled_Buffer controlled_buffer_44
  assign m5 = and_24_out ? ic_3_f5 : 1'bz;  // Controlled_Buffer controlled_buffer_45
  assign m4 = and_24_out ? ic_3_f4 : 1'bz;  // Controlled_Buffer controlled_buffer_46
  assign m4 = and_25_out ? ic_4_f4 : 1'bz;  // Controlled_Buffer controlled_buffer_47
  assign m4 = and_26_out ? ic_5_f4 : 1'bz;  // Controlled_Buffer controlled_buffer_48
  assign m0 = and_26_out ? ic_5_f0 : 1'bz;  // Controlled_Buffer controlled_buffer_49
  assign m6 = and_24_out ? ic_3_f6 : 1'bz;  // Controlled_Buffer controlled_buffer_50
  assign m5 = and_25_out ? ic_4_f5 : 1'bz;  // Controlled_Buffer controlled_buffer_51
  assign m5 = and_26_out ? ic_5_f5 : 1'bz;  // Controlled_Buffer controlled_buffer_52
  assign m6 = and_25_out ? ic_4_f6 : 1'bz;  // Controlled_Buffer controlled_buffer_53
  assign m6 = and_26_out ? ic_5_f6 : 1'bz;  // Controlled_Buffer controlled_buffer_54

  assign out_10 = out_8;

  // Other names for the same wires on the sheet: min_c[3:0] = out_3; Q4 = out_6[0]; Q3 = out_6[1]; Q2 = out_6[2];
  //   Q1 = out_6[3]; q4_t = out_7[0]; q3_t = out_7[1]; q2_t = out_7[2]; q1_t = out_7[3]; sec_c[3:0] = out_8

  // Notes on the sheet:
  //   in_1: initial=0x20
  //   in_2: initial=0x20
  //   будильник
  //   обновление состояния
  //   часы: основное отображение времени
  //   если +1 минута - останов часов
  //   продолжаем отсчет при переходе в S0
  //   am-pm
  //   am-pm
  //   звуковой сигнал каждый час в 10 минут
  //   секундомер
  //   переход 11- 0
  //   отображение режима С - clock
  //   отображение режима S - stopwatch
  //   отображение режима b -  будильник
endmodule

module ic (
  input  [3:0] simbols,
  output [6:0] out_2,
  output f6,
  output f5,
  output f4,
  output f0,
  output f1,
  output f2,
  output f3
);

  ROM #(.addrWidth(4), .dataWidth(7)) rom_1 (.addr(simbols), .data({f0, f1, f2, f3, f4, f5, f6}));
  Hex_Digit_Display hex_digit_display_1 (.value(simbols));  // open: dp
  _7_Segment_Display #(.decimalPoint("false")) u_7_segment_display_1 (
    .g(f0), .f(f1), .a(f2), .b(f3), .e(f6), .d(f5), .c(f4));

  assign out_2 = {f0, f1, f2, f3, f4, f5, f6};

  // Notes on the sheet:
  //   contents of rom_1 (hex, n*v repeats v):
  //   3f c 5b 5e 6c 76 77 1c 7f 7e 7d 79 67 33
  //   индикаторный преобразователь
endmodule

module FiL (
  input  x1,
  input  x2,
  input  q1,
  input  q2,
  input  q3,
  input  q4,
  output i1,
  output L1,
  output EQ1,
  output i3,
  output L2,
  output EQ4,
  output EQ3,
  output L3,
  output i4,
  output L4,
  output L5,
  output EQ2,
  output L6,
  output i2,
  output L7,
  output L8,
  output L9
);

  wire and_1_out, and_2_out, and_4_out, and_5_out, and_6_out, and_7_out, and_8_out, and_9_out, and_10_out,
       and_11_out, and_12_out, and_13_out, and_14_out, and_15_out, and_17_out, and_18_out, and_20_out,
       and_21_out, and_24_out, and_25_out, and_26_out, and_27_out, and_28_out, and_29_out, and_30_out,
       and_31_out, and_32_out, and_33_out, and_34_out, and_35_out, and_36_out, and_37_out, and_38_out,
       and_39_out, and_40_out, and_41_out, and_42_out, and_43_out, and_44_out, and_45_out, and_46_out,
       and_47_out, and_48_out, and_49_out, and_50_out, and_51_out, and_52_out, and_53_out, and_54_out, Nq1,
       Nq2, Nq3, Nq4, Nx1, Nx2;

  not not_1 (Nx1, x1);
  not not_2 (Nx2, x2);
  not not_3 (Nq1, q1);
  not not_4 (Nq2, q2);
  not not_5 (Nq3, q3);
  not not_6 (Nq4, q4);
  and and_1 (and_1_out, Nx1, x2, Nq1, Nq2, Nq3, q4);
  and and_2 (and_2_out, Nx1, Nx2, q1, Nq2, Nq3, Nq4);
  and and_3 (i3, x1, Nx2, Nq1, q2, Nq3, Nq4);
  and and_4 (and_4_out, Nx1, Nx2, Nq1, Nq2, q3, Nq4);
  and and_5 (and_5_out, x1, x2, q1, Nq2, Nq3, q4);
  and and_6 (and_6_out, Nx1, x2, Nq1, Nq2, q3, Nq4);
  and and_7 (and_7_out, Nx1, Nx2, q1, Nq2, Nq3, q4);
  or or_1 (i1, and_1_out, and_2_out);
  or or_2 (i4, and_4_out, and_5_out);
  or or_3 (i2, and_6_out, and_7_out);
  and and_8 (and_8_out, Nq1, Nq2, Nq4);
  and and_9 (and_9_out, Nq1, q2, q3);
  and and_10 (and_10_out, q1, Nq2, Nq3, q4);
  and and_11 (and_11_out, Nq1, q2);
  and and_12 (and_12_out, Nq1, q4);
  and and_13 (and_13_out, Nq2, Nq3, Nq4);
  and and_14 (and_14_out, Nq1, q2, Nq3);
  and and_15 (and_15_out, Nq1, Nq2, q3, q4);
  and and_16 (L4, Nq1, q2, Nq3, q4);
  and and_17 (and_17_out, q1, Nq2, Nq3);
  and and_18 (and_18_out, Nq1, q2, q3);
  and and_19 (L7, Nq1, q2, q3, q4);
  and and_20 (and_20_out, Nq1, Nq2, Nq3, q4);
  or or_4 (L9, and_20_out, and_21_out);
  and and_21 (and_21_out, Nq1, Nq2, q3, Nq4);
  or or_5 (L1, and_8_out, and_9_out, and_10_out);
  or or_6 (L2, and_11_out, and_12_out, and_13_out);
  or or_7 (L3, and_14_out, and_15_out);
  or or_8 (L6, and_17_out, and_18_out);
  and and_22 (L5, Nq1, q2, Nq3, Nq4);
  and and_23 (L8, q1, Nq2, q3, Nq4);
  and and_24 (and_24_out, q1, Nq3, Nq4);
  and and_25 (and_25_out, Nx1, Nx2, q1);
  and and_26 (and_26_out, x1, x2, q1, q4);
  and and_27 (and_27_out, x1, x2, Nq2, Nq3, Nq4);
  and and_28 (and_28_out, Nx1, x2, q2, q3, Nq4);
  and and_29 (and_29_out, q2, q3, q4);
  and and_30 (and_30_out, Nx1, q3, q4);
  and and_31 (and_31_out, x1, Nx2, q1, q4);
  and and_32 (and_32_out, Nx1, x2, q1, q4);
  and and_33 (and_33_out, Nx1, Nx2, q2, q3);
  and and_34 (and_34_out, x1, Nx2, Nq1, Nq3, Nq4);
  or or_9 (EQ1, and_24_out, and_25_out, and_26_out, and_27_out, and_28_out);
  or or_10 (EQ2, and_29_out, and_30_out, and_31_out, and_32_out, and_33_out, and_34_out);
  and and_35 (and_35_out, q2, q4);
  and and_36 (and_36_out, Nx1, Nx2, q2);
  and and_37 (and_37_out, x1, Nx2, Nq3, q4);
  and and_38 (and_38_out, x1, Nq1, Nq2, Nq3);
  and and_39 (and_39_out, x2, Nq1, Nq3, Nq4);
  and and_40 (and_40_out, Nx1, x2, q1, q4);
  and and_41 (and_41_out, Nx1, Nx2, q3, Nq4);
  and and_42 (and_42_out, Nx2, Nq1, Nq3, q4);
  and and_43 (and_43_out, Nx1, x2, Nq1, Nq2, Nq4);
  or or_11 (EQ3, and_35_out, and_36_out, and_37_out, and_38_out, and_39_out, and_40_out, and_41_out, and_42_out, and_43_out);
  and and_44 (and_44_out, x2, q2, Nq3);
  and and_45 (and_45_out, q2, Nq3, q4);
  and and_46 (and_46_out, x1, x2, q1, q4);
  and and_47 (and_47_out, x1, q1, Nq3, Nq4);
  and and_48 (and_48_out, Nx1, x2, q2, q4);
  and and_49 (and_49_out, Nx1, x2, Nq1, Nq3);
  and and_50 (and_50_out, x2, q1, Nq3, Nq4);
  and and_51 (and_51_out, Nx1, Nx2, q1, q4);
  and and_52 (and_52_out, Nx1, Nx2, q2, Nq4);
  and and_53 (and_53_out, Nx1, Nq1, Nq3, Nq4);
  and and_54 (and_54_out, Nx1, Nx2, Nq2, q3, q4);
  or or_12 (EQ4, and_44_out, and_45_out, and_46_out, and_47_out, and_48_out, and_49_out, and_50_out, and_51_out, and_52_out, and_53_out, and_54_out);
endmodule

module music (
  input  [3:0] min_ed,
  input  [3:0] min_dec,
  input  L8,
  output [13:0] freq,
  output up,
  output m6,
  output m5,
  output m4,
  output m0,
  output m1,
  output m2,
  output m3
);

  wire comparator_1_eq, comparator_2_eq;
  wire [3:0] counter_1_q;

  Counter #(.max('h9), .trigger("falling"), .width(4)) counter_1 (
    .clk(L8), .Q(counter_1_q));  // open: clr, load, up, count, D, carry
  ROM #(.addrWidth(4), .dataWidth(14)) rom_1 (.addr(counter_1_q), .data(freq));
  ic ic_1 (.simbols(counter_1_q), .f6(m6), .f5(m5), .f4(m4), .f0(m0), .f1(m1), .f2(m2), .f3(m3));  // open: out_2
  Comparator #(.width(4)) comparator_1 (.a(min_ed), .b(4'b0000), .eq(comparator_1_eq));  // open: gt, lt
  Comparator #(.width(4)) comparator_2 (.a(min_dec), .b(4'b0001), .eq(comparator_2_eq));  // open: gt, lt
  and and_1 (up, comparator_1_eq, comparator_2_eq);

  // Notes on the sheet:
  //   contents of rom_1 (hex, n*v repeats v):
  //   c8 12c 190 1f4 258 2bc 320 384 3e8 44c
endmodule

module stopwatch (
  input  i3,
  input  clk,
  input  L3,
  input  a,
  input  L5,
  output [3:0] sec_ed,
  output [3:0] min_ed_t,
  output [3:0] sec_dec,
  output [3:0] min_dec_t
);

  wire and_1_out, and_2_out, counter_1_carry, counter_2_carry, counter_3_carry, counter_4_carry, or_1_out,
       s_r_ff_1_q;
  wire [2:0] counter_2_q, counter_4_q;
  wire [3:0] bit_extender_1_out, bit_extender_2_out, counter_1_q, counter_3_q, undriven, undriven_2;

  and and_1 (and_1_out, L3, a);
  S_R_Flip_Flop #(.trigger("falling")) s_r_ff_1 (
    .S(and_1_out), .Q(s_r_ff_1_q), .reset(L5), .preset(and_1_out));  // open: R, clk, Qn
  Counter #(.max('h9), .trigger("falling"), .width(4)) counter_1 (
    .clr(i3), .clk(and_2_out), .D(undriven), .carry(counter_1_carry), .Q(counter_1_q));  // open: load, up, count
  and and_2 (and_2_out, clk, s_r_ff_1_q);
  assign sec_ed = L3 ? counter_1_q : 4'bz;  // Controlled_Buffer controlled_buffer_1
  Counter #(.max('h5), .trigger("falling"), .width(3)) counter_2 (
    .clr(i3), .clk(counter_1_carry), .carry(counter_2_carry), .Q(counter_2_q));  // open: load, up, count, D
  assign bit_extender_1_out = {{1{1'b0}}, counter_2_q};  // Bit_Extender bit_extender_1
  assign sec_dec = L3 ? bit_extender_1_out : 4'bz;  // Controlled_Buffer controlled_buffer_2
  Counter #(.max('h9), .trigger("falling"), .width(4)) counter_3 (
    .clr(or_1_out), .clk(counter_2_carry), .D(undriven_2), .carry(counter_3_carry), .Q(counter_3_q));  // open: load, up, count
  assign min_ed_t = L3 ? counter_3_q : 4'bz;  // Controlled_Buffer controlled_buffer_3
  or or_1 (or_1_out, i3, counter_4_carry);
  Counter #(.max('h5), .trigger("falling"), .width(3)) counter_4 (
    .clr(or_1_out), .clk(counter_3_carry), .carry(counter_4_carry), .Q(counter_4_q));  // open: load, up, count, D
  assign bit_extender_2_out = {{1{1'b0}}, counter_4_q};  // Bit_Extender bit_extender_2
  assign min_dec_t = L3 ? bit_extender_2_out : 4'bz;  // Controlled_Buffer controlled_buffer_4

  // Notes on the sheet:
  //   секундомер
endmodule
