// Logisim project 2.lab2_alg.circ as structural Verilog: 2 circuits, main circuit main
module main (
  output [3:0] out_1,
  output [3:0] out_2,
  output [3:0] out_3,
  output [3:0] out_4,
  output x1,
  output x2
);

  wire a, and_1_out, and_2_out, and_3_out, and_4_out, and_5_out, and_6_out, and_7_out, and_11_out,
       and_12_out, and_13_out, and_14_out, and_15_out, and_16_out, and_17_out, and_18_out, and_19_out,
       and_20_out, and_21_out, b, c, clear, clear_a, clk, comparator_1_eq, comparator_2_eq, comparator_3_eq,
       comparator_4_eq, comparator_5_eq, comparator_6_eq, comparator_7_eq, comparator_8_eq, comparator_9_eq,
       comparator_10_eq, comparator_11_lt, comparator_12_eq, comparator_13_eq, comparator_14_eq,
       comparator_15_lt, comparator_16_eq, comparator_17_eq, comparator_17_lt, comparator_18_eq,
       controlled_buffer_5_out, controlled_buffer_6_out, controlled_buffer_8_out, counter_1_carry,
       counter_2_carry, counter_4_carry, counter_5_carry, counter_6_carry, counter_7_carry, counter_8_carry,
       counter_9_carry, counter_11_carry, counter_13_carry, counter_14_carry, counter_15_carry, d, d_ff_1_qn,
       h_clear, i1, i2, i3, i4, i5, i6, i7, isW, L1, L2, L3, L4, L5, L6, L7, L8, L9, L10, L11, mus_b, next_h,
       next_min, not_1_out, not_2_out, not_3_out, not_4_out, not_5_out, not_6_out, not_7_out, not_8_out,
       not_9_out, not_10_out, not_11_out, not_12_out, not_13_out, not_14_out, not_15_out, not_16_out,
       not_17_out, not_18_out, not_19_out, or_2_out, or_5_out, or_6_out, or_7_out, or_8_out, or_9_out,
       or_10_out, or_11_out, or_12_out, or_13_out, or_14_out, or_15_out, or_16_out, press, s_r_ff_1_q, sig,
       stop;
  wire [2:0] counter_3_q, counter_4_q, counter_10_q, counter_11_q, counter_12_q, counter_13_q, counter_15_q;
  wire [3:0] bit_extender_4_out, bit_extender_7_out, controlled_buffer_10_out, counter_1_q, counter_6_q,
       counter_8_q, counter_14_q, h_ed2, h_ed3, HDA, HDA_2, HDC, HDC_2, HEC, m_ed2, m_ed3, MDA, MDA_2, MDC,
       MDC_2, MDS, MEA, MEC, MES, multiplexer_1_out, multiplexer_2_out, multiplexer_3_out, multiplexer_4_out,
       multiplexer_5_out, multiplexer_6_out, multiplexer_7_out, multiplexer_8_out, SDS, SES, week;

  or or_1 (press, d, c, b, a);
  Counter #(.max('ha), .trigger("falling"), .width(4)) counter_1 (
    .clr(or_2_out), .clk(and_1_out), .carry(counter_1_carry), .Q(counter_1_q));  // open: load, up, count, D
  or or_2 (or_2_out, clear_a, counter_1_carry);
  and and_1 (and_1_out, b, L9, i4);
  Counter #(.max('ha), .trigger("falling"), .width(4)) counter_2 (
    .clr(counter_2_carry), .clk(and_2_out), .carry(counter_2_carry), .Q(m_ed3));  // open: load, up, count, D
  and and_2 (and_2_out, b, L9, i2);
  Formulas formulas_1 (
    .x1(x1), .x2(x2), .q1(out_2[3]), .q2(out_2[2]), .q3(out_2[1]), .q4(out_2[0]), .i1(i1), .i7(i7), .L1(L1),
    .L6(L6), .L2(L2), .L7(L7), .i2(i2), .EQ1(out_1[3]), .L8(L8), .L9(L9), .L3(L3), .EQ2(out_1[2]), .i3(i3),
    .i4(i4), .EQ4(out_1[0]), .EQ3(out_1[1]), .L10(L10), .L4(L4), .L11(L11), .i5(i5), .L5(L5), .i6(i6));
  or or_3 (x1, d, c);
  or or_4 (x2, d, b);
  assign h_ed3 = L4 ? counter_1_q : 4'bz;  // Controlled_Buffer controlled_buffer_1
  and and_3 (and_3_out, L2, not_1_out);
  assign MEA = L2 ? m_ed3 : 4'bz;  // Controlled_Buffer controlled_buffer_2
  not not_1 (not_1_out, L11);
  Counter #(.max('h2), .trigger("falling"), .width(3)) counter_3 (
    .clr(clear_a), .clk(counter_1_carry), .Q(counter_3_q));  // open: load, up, count, D, carry
  Register #(.trigger("falling"), .width(4)) register_1 (.D(out_1), .clk(press), .Q(out_2));  // open: en, clr
  Counter #(.max('h6), .trigger("falling"), .width(3)) counter_4 (
    .clr(counter_4_carry), .clk(counter_2_carry), .carry(counter_4_carry), .Q(counter_4_q));  // open: load, up, count, D
  Comparator #(.mode("unsigned"), .width(4)) comparator_1 (.a(m_ed3), .b(m_ed2), .eq(comparator_1_eq));  // open: gt, lt
  Comparator #(.mode("unsigned"), .width(4)) comparator_2 (.a(MDC_2), .b(MDA_2), .eq(comparator_2_eq));  // open: gt, lt
  Comparator #(.mode("unsigned"), .width(4)) comparator_3 (.a(h_ed3), .b(h_ed2), .eq(comparator_3_eq));  // open: gt, lt
  Comparator #(.mode("unsigned"), .width(4)) comparator_4 (.a(HDC_2), .b(HDA_2), .eq(comparator_4_eq));  // open: gt, lt
  Hex_Digit_Display hex_digit_display_1 (.value(week));  // open: dp
  Multiplexer #(.width(4)) multiplexer_1 (.in0(HDC), .in1(HDA), .out(multiplexer_1_out), .sel(L9));
  Comparator #(.mode("unsigned"), .width(4)) comparator_5 (
    .a(m_ed2), .b(4'b0101), .eq(comparator_5_eq));  // open: gt, lt
  Comparator #(.mode("unsigned"), .width(4)) comparator_6 (
    .a(MDC_2), .b(4'b0001), .eq(comparator_6_eq));  // open: gt, lt
  or or_5 (or_5_out, comparator_6_eq, comparator_7_eq);
  Comparator #(.mode("unsigned"), .width(4)) comparator_7 (
    .a(MDC_2), .b(4'b0100), .eq(comparator_7_eq));  // open: gt, lt
  Comparator #(.mode("unsigned"), .width(4)) comparator_8 (
    .a(m_ed2), .b(4'b0000), .eq(comparator_8_eq));  // open: gt, lt
  Comparator #(.mode("unsigned"), .width(4)) comparator_9 (
    .a(MDC_2), .b(4'b0000), .eq(comparator_9_eq));  // open: gt, lt
  or or_6 (or_6_out, comparator_9_eq, comparator_10_eq);
  Comparator #(.mode("unsigned"), .width(4)) comparator_10 (
    .a(MDC_2), .b(4'b0011), .eq(comparator_10_eq));  // open: gt, lt
  Hex_Digit_Display hex_digit_display_2 (.value(multiplexer_2_out));  // open: dp
  Hex_Digit_Display hex_digit_display_3 (.value(multiplexer_4_out));  // open: dp
  Multiplexer #(.width(4)) multiplexer_2 (.in0(multiplexer_1_out), .in1(MDS), .out(multiplexer_2_out), .sel(L6));
  Multiplexer #(.width(4)) multiplexer_3 (.in0(HEC), .in1(h_ed3), .out(multiplexer_3_out), .sel(L9));
  and and_4 (and_4_out, comparator_5_eq, or_5_out);
  and and_5 (and_5_out, comparator_8_eq, or_6_out);
  and and_6 (and_6_out, comparator_1_eq, comparator_2_eq, isW, comparator_3_eq, comparator_4_eq);
  Button u_a (.out(a));
  Button u_b (.out(b));
  Hex_Digit_Display hex_digit_display_4 (.value(multiplexer_6_out));  // open: dp
  Multiplexer #(.width(4)) multiplexer_4 (.in0(multiplexer_3_out), .in1(MES), .out(multiplexer_4_out), .sel(L6));
  assign MDA_2 = {{1{1'b0}}, counter_4_q};  // Bit_Extender bit_extender_1
  assign MDA = L2 ? MDA_2 : 4'bz;  // Controlled_Buffer controlled_buffer_3
  D_Flip_Flop d_ff_1 (.D(d_ff_1_qn), .clk(and_7_out), .Q(isW), .Qn(d_ff_1_qn));  // open: preset, reset
  and and_7 (and_7_out, L10, b);
  assign HDA_2 = {{1{1'b0}}, counter_3_q};  // Bit_Extender bit_extender_2
  assign HDA = L5 ? HDA_2 : 4'bz;  // Controlled_Buffer controlled_buffer_4
  Comparator #(.mode("unsigned"), .width(4)) comparator_11 (
    .a(out_4), .b(4'b1010), .lt(comparator_11_lt));  // open: gt, eq
  Comparator #(.mode("unsigned"), .width(4)) comparator_12 (
    .a(out_3), .b(4'b0000), .eq(comparator_12_eq));  // open: gt, lt
  Button u_d (.out(d));
  Button u_c (.out(c));
  Hex_Digit_Display hex_digit_display_5 (.value(multiplexer_5_out), .dp(multiplexer_5_out[0]));
  Multiplexer #(.width(4)) multiplexer_5 (.in0(multiplexer_7_out), .in1(MEA), .out(multiplexer_5_out), .sel(L9));
  Multiplexer #(.width(4)) multiplexer_6 (.in0(multiplexer_8_out), .in1(MDA), .out(multiplexer_6_out), .sel(L9));
  Multiplexer #(.width(4)) multiplexer_7 (.in0(MEC), .in1(SES), .out(multiplexer_7_out), .sel(L6));
  Multiplexer #(.width(4)) multiplexer_8 (.in0(MDC), .in1(SDS), .out(multiplexer_8_out), .sel(L6));
  or or_7 (or_7_out, and_4_out, and_5_out);
  Comparator #(.mode("unsigned"), .width(4)) comparator_13 (
    .a(4'b0100), .b(h_ed3), .eq(comparator_13_eq));  // open: gt, lt
  Comparator #(.mode("unsigned"), .width(4)) comparator_14 (
    .a(4'b0010), .b(HDA_2), .eq(comparator_14_eq));  // open: gt, lt
  and and_8 (mus_b, comparator_11_lt, comparator_12_eq, and_6_out);
  Comparator #(.mode("unsigned"), .width(4)) comparator_15 (
    .a(out_4), .b(4'b0001), .lt(comparator_15_lt));  // open: gt, eq
  Comparator #(.mode("unsigned"), .width(4)) comparator_16 (
    .a(out_3), .b(4'b0000), .eq(comparator_16_eq));  // open: gt, lt
  and and_9 (clear_a, comparator_13_eq, comparator_14_eq);
  LED led_1 (.in(L11));
  LED led_2 (.in(L6));
  LED led_3 (.in(sig));
  LED led_4 (.in(isW));
  LED led_5 (.in(mus_b));
  and and_10 (sig, comparator_15_lt, comparator_16_eq, or_7_out);
  Clock clock_1 (.out(clk));
  or or_8 (or_8_out, clear, counter_5_carry);
  and and_11 (and_11_out, a, i4);
  and and_12 (and_12_out, a, i1);
  S_R_Flip_Flop s_r_ff_1 (.S(and_13_out), .Q(s_r_ff_1_q), .reset(i6), .preset(and_13_out));  // open: R, clk, Qn
  and and_13 (and_13_out, L6, b);
  not not_2 (not_2_out, stop);
  and and_14 (and_14_out, a, i2);
  or or_9 (or_9_out, and_14_out, next_min);
  Counter #(.max('ha), .trigger("falling"), .width(4)) counter_5 (
    .clr(or_8_out), .clk(or_10_out), .carry(counter_5_carry), .Q(h_ed2));  // open: load, up, count, D
  or or_10 (or_10_out, next_h, and_11_out);
  Counter #(.max('h7), .trigger("falling"), .width(4)) counter_6 (
    .clr(counter_6_carry), .clk(or_11_out), .carry(counter_6_carry), .Q(counter_6_q));  // open: load, up, count, D
  or or_11 (or_11_out, and_12_out, controlled_buffer_5_out);
  assign controlled_buffer_5_out = not_3_out ? clear : 1'bz;  // Controlled_Buffer controlled_buffer_5
  not not_3 (not_3_out, i4);
  not not_4 (not_4_out, L8);
  and and_15 (and_15_out, clk, not_2_out);
  Counter #(.max('ha), .trigger("falling"), .width(4)) counter_7 (
    .clr(counter_7_carry), .clk(or_9_out), .carry(counter_7_carry), .Q(m_ed2));  // open: load, up, count, D
  Counter #(.max('h9), .trigger("falling"), .width(4)) counter_8 (
    .clr(i6), .clk(and_16_out), .carry(counter_8_carry), .Q(counter_8_q));  // open: load, up, count, D
  and and_16 (and_16_out, s_r_ff_1_q, not_4_out, clk);
  Counter #(.max('h9), .trigger("falling"), .width(4)) counter_9 (
    .clk(and_15_out), .carry(counter_9_carry), .Q(out_4));  // open: clr, load, up, count, D
  not not_5 (not_5_out, i4);
  assign controlled_buffer_6_out = not_5_out ? counter_5_carry : 1'bz;  // Controlled_Buffer controlled_buffer_6
  assign HEC = L4 ? h_ed2 : 4'bz;  // Controlled_Buffer controlled_buffer_7
  not not_6 (not_6_out, i2);
  assign controlled_buffer_8_out = not_6_out ? counter_7_carry : 1'bz;  // Controlled_Buffer controlled_buffer_8
  and and_17 (and_17_out, L2, not_7_out);
  assign MEC = L2 ? m_ed2 : 4'bz;  // Controlled_Buffer controlled_buffer_9
  and and_18 (and_18_out, i5, a);
  assign controlled_buffer_10_out = L1 ? counter_6_q : 4'bz;  // Controlled_Buffer controlled_buffer_10
  Adder #(.width(4)) adder_1 (.a(controlled_buffer_10_out), .b(4'b0001), .out(week));  // open: cin, cout
  assign SES = L6 ? counter_8_q : 4'bz;  // Controlled_Buffer controlled_buffer_11
  and and_19 (and_19_out, a, i3);
  or or_12 (or_12_out, and_19_out, controlled_buffer_8_out);
  not not_7 (not_7_out, L11);
  Counter #(.max('h2), .trigger("falling"), .width(3)) counter_10 (
    .clr(h_clear), .clk(or_13_out), .Q(counter_10_q));  // open: load, up, count, D, carry
  or or_13 (or_13_out, controlled_buffer_6_out, and_18_out);
  Counter #(.max('h5), .trigger("falling"), .width(3)) counter_11 (
    .clr(i6), .clk(counter_8_carry), .carry(counter_11_carry), .Q(counter_11_q));  // open: load, up, count, D
  Counter #(.max('h6), .trigger("falling"), .width(3)) counter_12 (
    .clr(next_min), .clk(counter_9_carry), .carry(next_min), .Q(counter_12_q));  // open: load, up, count, D
  Counter #(.max('h6), .trigger("falling"), .width(3)) counter_13 (
    .clr(counter_13_carry), .clk(or_12_out), .carry(counter_13_carry), .Q(counter_13_q));  // open: load, up, count, D
  assign HDC_2 = {{1{1'b0}}, counter_10_q};  // Bit_Extender bit_extender_3
  assign HDC = L5 ? HDC_2 : 4'bz;  // Controlled_Buffer controlled_buffer_12
  assign bit_extender_4_out = {{1{1'b0}}, counter_11_q};  // Bit_Extender bit_extender_4
  assign SDS = L6 ? bit_extender_4_out : 4'bz;  // Controlled_Buffer controlled_buffer_13
  assign out_3 = {{1{1'b0}}, counter_12_q};  // Bit_Extender bit_extender_5
  not not_8 (not_8_out, i3);
  assign next_h = not_8_out ? counter_13_carry : 1'bz;  // Controlled_Buffer controlled_buffer_14
  assign MDC_2 = {{1{1'b0}}, counter_13_q};  // Bit_Extender bit_extender_6
  assign MDC = L3 ? MDC_2 : 4'bz;  // Controlled_Buffer controlled_buffer_15
  Counter #(.max('h9), .trigger("falling"), .width(4)) counter_14 (
    .clr(or_16_out), .clk(counter_11_carry), .carry(counter_14_carry), .Q(counter_14_q));  // open: load, up, count, D
  Comparator #(.mode("unsigned"), .width(4)) comparator_17 (
    .a(4'b0100), .b(h_ed2), .eq(comparator_17_eq), .lt(comparator_17_lt));  // open: gt
  Comparator #(.mode("unsigned"), .width(4)) comparator_18 (
    .a(4'b0010), .b(HDC_2), .eq(comparator_18_eq));  // open: gt, lt
  or or_14 (or_14_out, comparator_17_eq, comparator_17_lt);
  assign MES = L6 ? counter_14_q : 4'bz;  // Controlled_Buffer controlled_buffer_16
  not not_9 (not_9_out, L9);
  not not_10 (not_10_out, L1);
  not not_11 (not_11_out, L2);
  not not_12 (not_12_out, L3);
  or or_15 (or_15_out, not_10_out, not_11_out, not_12_out, not_13_out, not_14_out);
  not not_13 (not_13_out, L4);
  not not_14 (not_14_out, L5);
  not not_15 (not_15_out, L6);
  not not_16 (not_16_out, i5);
  and and_20 (and_20_out, or_14_out, comparator_18_eq);
  assign clear = not_16_out ? and_20_out : 1'bz;  // Controlled_Buffer controlled_buffer_17
  not not_17 (not_17_out, i4);
  assign h_clear = not_17_out ? and_20_out : 1'bz;  // Controlled_Buffer controlled_buffer_18
  Counter #(.max('h6), .trigger("falling"), .width(3)) counter_15 (
    .clr(or_16_out), .clk(counter_14_carry), .carry(counter_15_carry), .Q(counter_15_q));  // open: load, up, count, D
  and and_21 (and_21_out, or_15_out, not_9_out, not_15_out);
  not not_18 (not_18_out, L11);
  not not_19 (not_19_out, L9);
  or or_16 (or_16_out, i6, counter_15_carry);
  and and_22 (stop, and_21_out, not_18_out, not_19_out);
  assign bit_extender_7_out = {{1{1'b0}}, counter_15_q};  // Bit_Extender bit_extender_7
  assign MDS = L6 ? bit_extender_7_out : 4'bz;  // Controlled_Buffer controlled_buffer_19
  // Pins of 1 and 4 bits meet at multiplexer_5_out

  // Other names for the same wires on the sheet: HEA[3:0] = h_ed3; EQ4 = out_1[0]; EQ3 = out_1[1]; EQ2 = out_1[2];
  //   EQ1 = out_1[3]; q4 = out_2[0]; q3 = out_2[1]; q2 = out_2[2]; q1 = out_2[3]; SDC[3:0] = out_3; SEC[3:0] = out_4

  // Notes on the sheet:
  //   будильник
  //   обновление состояния
  //   звуковой сигнал каждые 15 мин
  //   энергосбережение
  //   секундомер
  //   сигнал 15 мин
  //   вкл будильник
  //   сигнал будильник
  //   секундомер
endmodule

module Formulas (
  input  x1,
  input  x2,
  input  q1,
  input  q2,
  input  q3,
  input  q4,
  output i1,
  output i7,
  output L1,
  output L6,
  output L2,
  output L7,
  output i2,
  output EQ1,
  output L8,
  output L9,
  output L3,
  output EQ2,
  output i3,
  output i4,
  output EQ4,
  output EQ3,
  output L10,
  output L4,
  output L11,
  output i5,
  output L5,
  output i6
);

  wire and_1_out, and_2_out, and_3_out, and_4_out, and_5_out, and_6_out, and_7_out, and_8_out, and_9_out,
       and_10_out, and_11_out, and_12_out, and_13_out, and_14_out, and_15_out, and_16_out, and_17_out,
       and_18_out, and_19_out, and_20_out, and_21_out, and_22_out, and_23_out, and_24_out, and_25_out,
       and_26_out, and_27_out, and_28_out, and_29_out, and_30_out, and_31_out, and_32_out, and_33_out,
       and_34_out, and_35_out, and_36_out, and_37_out, and_38_out, and_39_out, and_40_out, and_42_out,
       and_43_out, and_44_out, and_45_out, and_46_out, and_47_out, and_48_out, and_49_out, and_50_out,
       and_51_out, and_52_out, and_53_out, and_54_out, and_55_out, and_56_out, and_57_out, and_60_out,
       and_61_out, and_65_out, and_66_out, and_67_out, and_68_out, and_69_out, and_70_out, and_71_out,
       and_72_out, and_73_out, and_75_out, and_76_out, Nq1, Nq2, Nq3, Nq4, Nx1, Nx2;

  not not_1 (Nx1, x1);
  not not_2 (Nx2, x2);
  not not_3 (Nq1, q1);
  not not_4 (Nq2, q2);
  not not_5 (Nq3, q3);
  not not_6 (Nq4, q4);
  and and_1 (and_1_out, q1, q2);
  and and_2 (and_2_out, x1, q1, Nq4);
  and and_3 (and_3_out, x2, q1, Nq4);
  and and_4 (and_4_out, q1, q3, q4);
  and and_5 (and_5_out, q1, Nq3, Nq4);
  and and_6 (and_6_out, Nx1, Nx2, q1, q4);
  and and_7 (and_7_out, x1, x2, Nq2, Nq3, Nq4);
  and and_8 (and_8_out, Nx1, x2, q2, q3, q4);
  or or_1 (EQ1, and_1_out, and_2_out, and_3_out, and_4_out, and_5_out, and_6_out, and_7_out, and_8_out);
  and and_9 (and_9_out, q2, Nq3, Nq4);
  and and_10 (and_10_out, Nq1, q2, Nq3);
  and and_11 (and_11_out, x1, q1, q3, Nq4);
  and and_12 (and_12_out, Nx1, Nx2, q2, Nq4);
  and and_13 (and_13_out, Nx1, x2, q1, q2);
  and and_14 (and_14_out, x1, q1, Nq2, Nq3, q4);
  and and_15 (and_15_out, x1, Nq1, Nq2, q3, q4);
  and and_16 (and_16_out, Nx1, x2, Nq1, Nq3, Nq4);
  and and_17 (and_17_out, x2, Nq1, Nq2, q3, q4);
  and and_18 (and_18_out, x2, q1, Nq2, Nq3, q4);
  or or_2 (EQ2, and_9_out, and_10_out, and_11_out, and_12_out, and_13_out, and_14_out, and_15_out, and_16_out, and_17_out, and_18_out);
  and and_19 (and_19_out, x1, Nx2, Nq2, Nq1, Nq4);
  and and_20 (and_20_out, x1, q1, Nq3, Nq2);
  and and_21 (and_21_out, x1, q2, Nq3, Nq4);
  and and_22 (and_22_out, Nx1, x2, q1, q4);
  and and_23 (and_23_out, Nx1, x2, Nq2, Nq4);
  and and_24 (and_24_out, Nx2, q1, q2, Nq4);
  and and_25 (and_25_out, q1, Nq2, Nq3, Nq4);
  and and_26 (and_26_out, x1, q3, Nq2, Nq1, Nq4);
  and and_27 (and_27_out, x2, Nq1, q2, Nq3, Nq4);
  and and_28 (and_28_out, Nx1, Nx2, Nq1, q2, Nq3, q4);
  and and_29 (and_29_out, Nx1, Nx2, Nq1, Nq2, q3, q4);
  or or_3 (EQ4, and_20_out, and_21_out, and_22_out, and_23_out, and_24_out, and_19_out, and_25_out, and_26_out, and_27_out, and_28_out, and_29_out);
  and and_30 (and_30_out, x1, q1, q4);
  and and_31 (and_31_out, x1, q2, Nq3, q4);
  and and_32 (and_32_out, Nx1, x2, q1, q3);
  and and_33 (and_33_out, x2, Nq1, Nq2, Nq4);
  and and_34 (and_34_out, x2, q1, Nq2, q4);
  and and_35 (and_35_out, Nx2, q1, q2, q4);
  and and_36 (and_36_out, Nq1, Nq2, q3, Nq4);
  and and_37 (and_37_out, Nq1, Nq2, Nx1, Nq4);
  and and_38 (and_38_out, Nx1, Nx2, q2, q3, Nq4);
  and and_39 (and_39_out, Nx1, Nx2, q3, Nq2, q4);
  and and_40 (and_40_out, Nq1, x2, q2, Nq3, q4);
  or or_4 (EQ3, and_30_out, and_31_out, and_32_out, and_33_out, and_34_out, and_35_out, and_36_out, and_37_out, and_38_out, and_39_out, and_40_out);
  and and_41 (L1, Nq1, Nq4, Nq2);
  and and_42 (and_42_out, q1, Nq2);
  and and_43 (and_43_out, q1, Nq4, Nq3);
  and and_44 (and_44_out, Nq2, Nq4, Nq3);
  and and_45 (and_45_out, Nq1, q4, q3);
  and and_46 (and_46_out, q1, Nq2);
  and and_47 (and_47_out, Nq3, Nq4);
  and and_48 (and_48_out, Nq1, q2, q3, q4);
  and and_49 (and_49_out, q1, Nq2, q3);
  and and_50 (and_50_out, q2, q4, Nq3);
  and and_51 (and_51_out, Nq1, Nq2, Nq3, Nq4);
  and and_52 (and_52_out, q1, Nq2, q3);
  and and_53 (and_53_out, Nq1, Nq2, Nq3, Nq4);
  and and_54 (and_54_out, q1, q2, Nq3, q4);
  and and_55 (and_55_out, Nq1, q2, q3, Nq4);
  or or_5 (L2, and_42_out, and_43_out, and_44_out, and_45_out);
  or or_6 (L3, and_46_out, and_47_out, and_48_out);
  or or_7 (L4, and_49_out, and_50_out, and_51_out);
  or or_8 (L5, and_52_out, and_53_out, and_54_out, and_55_out);
  and and_56 (and_56_out, q1, Nq2, Nq3);
  and and_57 (and_57_out, Nq1, q2, q3, q4);
  and and_58 (L7, q1, Nq2, Nq3, Nq4);
  and and_59 (L8, q1, Nq2, Nq3, q4);
  and and_60 (and_60_out, q1, q2, Nq3);
  and and_61 (and_61_out, Nq2, q1, q3);
  and and_62 (L10, q1, Nq2, q3, q4);
  and and_63 (L11, Nq1, Nq2, Nq3, q4);
  or or_9 (L6, and_56_out, and_57_out);
  or or_10 (L9, and_60_out, and_61_out);
  and and_64 (i1, Nx1, Nx2, Nq1, Nq2, q3, Nq4);
  and and_65 (and_65_out, Nx1, x2, q1, q2, Nq4);
  and and_66 (and_66_out, Nx1, Nx2, Nq1, Nq2, q3, q4);
  and and_67 (and_67_out, Nx1, x2, q1, q2, Nq4);
  and and_68 (and_68_out, Nx1, Nx2, Nq1, q2, Nq3, Nq4);
  and and_69 (and_69_out, Nx1, x2, q1, q2, q4);
  and and_70 (and_70_out, Nx1, Nx2, q3, q2, Nq4);
  and and_71 (and_71_out, Nx1, x2, Nq1, Nq2, Nq3, Nq4);
  and and_72 (and_72_out, x1, q1, Nq3, Nq2, q4);
  and and_73 (and_73_out, Nq3, x2, q1, Nq2, q4);
  or or_11 (i2, and_65_out, and_66_out);
  or or_12 (i3, and_67_out, and_68_out);
  or or_13 (i5, and_69_out, and_70_out);
  or or_14 (i6, and_71_out, and_72_out, and_73_out);
  and and_74 (i7, Nq1, Nq2, Nq3, q4);
  and and_75 (and_75_out, Nx1, x2, q1, q2, q4);
  and and_76 (and_76_out, Nx1, Nx2, Nq1, q2, Nq3, q4);
  or or_15 (i4, and_75_out, and_76_out);
endmodule
