// Logisim project 3.lab2.circ as structural Verilog: 2 circuits, main circuit main
module main (
  output x1,
  output x2,
  output [2:0] out_3,
  output [2:0] out_4,
  output [3:0] out_5,
  output [3:0] out_6,
  output [7:0] out_7,
  output [7:0] out_8,
  output [7:0] out_9,
  output [2:0] out_10,
  output [3:0] out_11
);

  wire and_1_out, and_2_out, and_4_out, and_5_out, and_6_out, and_7_out, and_8_out, and_9_out, b, clear, clk,
       clk_h, comparator_1_eq, comparator_2_eq, comparator_3_eq, comparator_4_eq, comparator_5_eq,
       comparator_6_eq, comparator_7_lt, comparator_8_eq, comparator_9_eq, comparator_10_eq,
       controlled_buffer_4_out, controlled_buffer_7_out, counter_3_carry, counter_4_carry, counter_5_carry,
       counter_6_carry, counter_7_carry, counter_9_carry, counter_10_carry, counter_11_carry,
       counter_12_carry, i1, i2, i3, i4, L1, L2, L3, L4, L5, L6, L7, L8, music, not_1_out, not_2_out,
       not_3_out, or_1_out, or_2_out, or_3_out, or_7_out, or_8_out, or_9_out, or_11_out, p, press, sec, SW,
       undriven;
  wire [2:0] counter_2_q, counter_7_q, counter_8_q, counter_9_q, counter_12_q, counter_13_q;
  wire [3:0] bit_extender_3_out, bit_extender_5_out, bit_extender_7_out, controlled_buffer_6_out,
       counter_5_q, counter_6_q, counter_11_q, h_d, h_dec, h_e, h_ed, h_ed2, hd_d, hd_e, m1, m2, min_d,
       min_d_S, min_e, min_e_S, multiplexer_1_out, multiplexer_2_out, multiplexer_3_out, multiplexer_4_out,
       sec_d, sec_e, week;
  wire [7:0] bit_extender_1_out, bit_extender_2_out, multiplier_1_out;
  wire [7:3] divider_2_out;
  wire [7:4] divider_2_rem;

  Comparator #(.mode("unsigned"), .width(4)) comparator_1 (.a(m1), .b(4'b0101), .eq(comparator_1_eq));  // open: gt, lt
  Comparator #(.mode("unsigned"), .width(4)) comparator_2 (.a(m2), .b(4'b0001), .eq(comparator_2_eq));  // open: gt, lt
  Comparator #(.mode("unsigned"), .width(4)) comparator_3 (.a(m2), .b(4'b0100), .eq(comparator_3_eq));  // open: gt, lt
  Comparator #(.mode("unsigned"), .width(4)) comparator_4 (.a(m1), .b(4'b0000), .eq(comparator_4_eq));  // open: gt, lt
  Comparator #(.mode("unsigned"), .width(4)) comparator_5 (.a(m2), .b(4'b0000), .eq(comparator_5_eq));  // open: gt, lt
  Comparator #(.mode("unsigned"), .width(4)) comparator_6 (.a(m2), .b(4'b0011), .eq(comparator_6_eq));  // open: gt, lt
  or or_1 (or_1_out, comparator_2_eq, comparator_3_eq);
  or or_2 (or_2_out, comparator_5_eq, comparator_6_eq);
  and and_1 (and_1_out, comparator_1_eq, or_1_out);
  and and_2 (and_2_out, comparator_4_eq, or_2_out);
  assign bit_extender_1_out = {{4{1'b0}}, h_dec};  // Bit_Extender bit_extender_1
  assign bit_extender_2_out = {{4{1'b0}}, h_ed};  // Bit_Extender bit_extender_2
  Multiplier multiplier_1 (.a(bit_extender_1_out), .b(8'ha), .out(multiplier_1_out));  // open: cin, cout
  Register #(.trigger("falling"), .width(3)) register_1 (.D(out_3), .clk(press), .Q(out_4));  // open: en, clr
  Comparator #(.mode("unsigned"), .width(4)) comparator_7 (
    .a(out_6), .b(4'b0001), .lt(comparator_7_lt));  // open: gt, eq
  Comparator #(.mode("unsigned"), .width(4)) comparator_8 (
    .a(out_5), .b(4'b0000), .eq(comparator_8_eq));  // open: gt, lt
  or or_3 (or_3_out, and_1_out, and_2_out);
  Adder adder_1 (.a(bit_extender_2_out), .b(multiplier_1_out), .out(out_7));  // open: cin, cout
  Adder adder_2 (.a(out_7), .b(8'h3), .out(out_8));  // open: cin, cout
  Func_block func_block_1 (
    .x1(x1), .x2(x2), .q1(out_4[2]), .q2(out_4[1]), .q3(out_4[0]), .i1(i1), .L1(L1), .FQ1(out_3[2]), .L2(L2),
    .i2(i2), .i3(i3), .L3(L3), .FQ2(out_3[1]), .i4(i4), .L4(L4), .L5(L5), .L6(L6), .L7(L7), .FQ3(out_3[0]),
    .L8(L8));
  and and_3 (music, comparator_7_lt, comparator_8_eq, or_3_out);
  Divider divider_1 (.a(out_8), .b(8'h18), .rem(out_9));  // open: out, upper
  Divider divider_2 (.a(out_9), .b(8'ha), .out({divider_2_out, out_10}), .rem({divider_2_rem, out_11}));  // open: upper
  or or_4 (press, p, b, SW);
  Counter #(.max('ha), .trigger("falling"), .width(4)) counter_1 (
    .load(1'b1), .clk(clk), .D(out_11), .Q(h_ed2));  // open: clr, up, count, carry
  or or_5 (x1, p, SW);
  or or_6 (x2, p, b);
  LED led_1 (.in(music));
  Hex_Digit_Display hex_digit_display_1 (.value(week));  // open: dp
  Multiplexer #(.width(4)) multiplexer_1 (.in0(h_e), .in1(hd_e), .out(multiplexer_1_out), .sel(L8));
  Multiplexer #(.width(4)) multiplexer_2 (.in0(h_d), .in1(hd_d), .out(multiplexer_2_out), .sel(L8));
  assign hd_e = L3 ? h_ed2 : 4'bz;  // Controlled_Buffer controlled_buffer_1
  Button u_b (.out(b));
  Hex_Digit_Display hex_digit_display_2 (.value(multiplexer_2_out));  // open: dp
  Hex_Digit_Display hex_digit_display_3 (.value(multiplexer_1_out));  // open: dp
  Counter #(.max('h2), .trigger("falling"), .width(3)) counter_2 (
    .clr(undriven), .load(1'b1), .clk(clk), .D(out_10), .Q(counter_2_q));  // open: up, count, carry
  Button u_p (.out(p));
  Hex_Digit_Display hex_digit_display_4 (.value(multiplexer_3_out));  // open: dp
  Multiplexer #(.width(4)) multiplexer_3 (.in0(min_d), .in1(min_d_S), .out(multiplexer_3_out), .sel(L4));
  Button u_SW (.out(SW));
  Hex_Digit_Display hex_digit_display_5 (.value(multiplexer_4_out), .dp(multiplexer_4_out[0]));
  Multiplexer #(.width(4)) multiplexer_4 (.in0(min_e), .in1(min_e_S), .out(multiplexer_4_out), .sel(L4));
  Hex_Digit_Display hex_digit_display_6 (.value(sec_d));  // open: dp
  Hex_Digit_Display hex_digit_display_7 (.value(sec_e));  // open: dp
  assign bit_extender_3_out = {{1{1'b0}}, counter_2_q};  // Bit_Extender bit_extender_3
  assign hd_d = L3 ? bit_extender_3_out : 4'bz;  // Controlled_Buffer controlled_buffer_2
  and and_4 (and_4_out, i1, b);
  Clock clock_1 (.out(clk));
  Counter #(.max('ha), .width(4)) counter_3 (
    .clr(counter_3_carry), .clk(or_7_out), .carry(counter_3_carry), .Q(m1));  // open: load, up, count, D
  or or_7 (or_7_out, sec, and_4_out);
  and and_5 (and_5_out, clk, not_1_out);
  not not_1 (not_1_out, L5);
  Counter #(.max('ha), .trigger("falling"), .width(4)) counter_4 (
    .clr(counter_4_carry), .clk(and_5_out), .carry(counter_4_carry), .Q(out_6));  // open: load, up, count, D
  and and_6 (and_6_out, i4, b);
  Counter #(.max('h9), .width(4)) counter_5 (
    .clr(and_6_out), .clk(and_7_out), .carry(counter_5_carry), .Q(counter_5_q));  // open: load, up, count, D
  and and_7 (and_7_out, L7, clk);
  assign min_e = L1 ? m1 : 4'bz;  // Controlled_Buffer controlled_buffer_3
  and and_8 (and_8_out, i3, b);
  or or_8 (or_8_out, and_8_out, controlled_buffer_4_out);
  assign controlled_buffer_4_out = not_2_out ? clear : 1'bz;  // Controlled_Buffer controlled_buffer_4
  not not_2 (not_2_out, i2);
  Counter #(.max('h7), .width(4)) counter_6 (
    .clr(counter_6_carry), .clk(or_8_out), .carry(counter_6_carry), .Q(counter_6_q));  // open: load, up, count, D
  Counter #(.max('h6), .width(3)) counter_7 (
    .clr(counter_7_carry), .clk(counter_3_carry), .carry(counter_7_carry), .Q(counter_7_q));  // open: load, up, count, D
  assign sec_e = L4 ? counter_5_q : 4'bz;  // Controlled_Buffer controlled_buffer_5
  Counter #(.max('h6), .trigger("falling"), .width(3)) counter_8 (
    .clr(sec), .clk(counter_4_carry), .carry(sec), .Q(counter_8_q));  // open: load, up, count, D
  Counter #(.max('h5), .trigger("falling"), .width(3)) counter_9 (
    .clr(and_6_out), .clk(counter_5_carry), .carry(counter_9_carry), .Q(counter_9_q));  // open: load, up, count, D
  assign controlled_buffer_6_out = L2 ? counter_6_q : 4'bz;  // Controlled_Buffer controlled_buffer_6
  not not_3 (not_3_out, i1);
  assign controlled_buffer_7_out = not_3_out ? counter_7_carry : 1'bz;  // Controlled_Buffer controlled_buffer_7
  assign m2 = {{1{1'b0}}, counter_7_q};  // Bit_Extender bit_extender_4
  Adder #(.width(4)) adder_3 (.a(controlled_buffer_6_out), .b(4'b0001), .out(week));  // open: cin, cout
  and and_9 (and_9_out, i2, p);
  assign min_d = L1 ? m2 : 4'bz;  // Controlled_Buffer controlled_buffer_8
  assign bit_extender_5_out = {{1{1'b0}}, counter_9_q};  // Bit_Extender bit_extender_5
  assign sec_d = L4 ? bit_extender_5_out : 4'bz;  // Controlled_Buffer controlled_buffer_9
  assign out_5 = {{1{1'b0}}, counter_8_q};  // Bit_Extender bit_extender_6
  Counter #(.max('ha), .width(4)) counter_10 (
    .clr(or_9_out), .clk(clk_h), .carry(counter_10_carry), .Q(h_ed));  // open: load, up, count, D
  or or_9 (or_9_out, clear, counter_10_carry);
  or or_10 (clk_h, and_9_out, controlled_buffer_7_out);
  Counter #(.max('h9), .trigger("falling"), .width(4)) counter_11 (
    .clr(or_11_out), .clk(counter_9_carry), .carry(counter_11_carry), .Q(counter_11_q));  // open: load, up, count, D
  assign min_e_S = L4 ? counter_11_q : 4'bz;  // Controlled_Buffer controlled_buffer_10
  assign h_e = L3 ? h_ed : 4'bz;  // Controlled_Buffer controlled_buffer_11
  Counter #(.max('h6), .trigger("falling"), .width(3)) counter_12 (
    .clr(or_11_out), .clk(counter_11_carry), .carry(counter_12_carry), .Q(counter_12_q));  // open: load, up, count, D
  or or_11 (or_11_out, and_6_out, counter_12_carry);
  Counter #(.max('h2), .width(3)) counter_13 (
    .clr(clear), .clk(counter_10_carry), .Q(counter_13_q));  // open: load, up, count, D, carry
  assign bit_extender_7_out = {{1{1'b0}}, counter_12_q};  // Bit_Extender bit_extender_7
  assign min_d_S = L4 ? bit_extender_7_out : 4'bz;  // Controlled_Buffer controlled_buffer_12
  assign h_dec = {{1{1'b0}}, counter_13_q};  // Bit_Extender bit_extender_8
  assign h_d = L3 ? h_dec : 4'bz;  // Controlled_Buffer controlled_buffer_13
  Comparator #(.mode("unsigned"), .width(4)) comparator_9 (
    .a(4'b0100), .b(h_ed), .eq(comparator_9_eq));  // open: gt, lt
  Comparator #(.mode("unsigned"), .width(4)) comparator_10 (
    .a(4'b0010), .b(h_dec), .eq(comparator_10_eq));  // open: gt, lt
  and and_10 (clear, comparator_9_eq, comparator_10_eq);
  // Pins of 1 and 4 bits meet at multiplexer_4_out

  // Other names for the same wires on the sheet: new_ed[3:0] = out_11; new_dec[2:0] = out_10; EQ3 = out_3[0];
  //   EQ2 = out_3[1]; EQ1 = out_3[2]; q3 = out_4[0]; q2 = out_4[1]; q1 = out_4[2]; s1[3:0] = out_6; s2[3:0] = out_5

  // Notes on the sheet:
  //   звуковой сигнал каждые 15 мин
  //   обновление состояния
  //   секундомер
endmodule

module Func_block (
  input  x1,
  input  x2,
  input  q1,
  input  q2,
  input  q3,
  output i1,
  output L1,
  output FQ1,
  output L2,
  output i2,
  output i3,
  output L3,
  output FQ2,
  output i4,
  output L4,
  output L5,
  output L6,
  output L7,
  output FQ3,
  output L8
);

  wire and_1_out, and_2_out, and_3_out, and_4_out, and_5_out, and_6_out, and_7_out, and_8_out, and_9_out,
       and_10_out, and_11_out, and_12_out, and_13_out, and_14_out, and_15_out, and_16_out, and_17_out,
       and_18_out, and_19_out, and_20_out, Nq1, Nq2, Nq3, Nx1, Nx2;

  not not_1 (Nx1, x1);
  not not_2 (Nx2, x2);
  not not_3 (Nq1, q1);
  not not_4 (Nq2, q2);
  not not_5 (Nq3, q3);
  and and_1 (and_1_out, q1, Nq2);
  and and_2 (and_2_out, q1, Nq3);
  and and_3 (and_3_out, Nx1, Nq2, Nq3);
  and and_4 (and_4_out, q1, q2, Nq3);
  and and_5 (and_5_out, x2, Nq1, q2);
  and and_6 (and_6_out, Nx2, q1, Nq2, q3);
  and and_7 (and_7_out, x1, x2, Nq1, Nq3);
  and and_8 (and_8_out, Nx2, q1, Nq3);
  and and_9 (and_9_out, Nx2, Nq2, Nq3);
  and and_10 (and_10_out, x2, Nq2, q3);
  and and_11 (and_11_out, Nx1, Nq1, q3);
  and and_12 (and_12_out, x1, x2, Nq1, q2, Nq3);
  or or_1 (FQ1, and_1_out, and_2_out, and_3_out);
  or or_2 (FQ2, and_4_out, and_5_out, and_6_out, and_7_out);
  or or_3 (FQ3, and_8_out, and_9_out, and_10_out, and_11_out, and_12_out);
  and and_13 (and_13_out, q2, q3);
  and and_14 (and_14_out, Nq2, Nq3);
  and and_15 (and_15_out, q2, q1);
  and and_16 (and_16_out, Nq1, Nq2, Nq3);
  and and_17 (and_17_out, Nq2, Nq1);
  and and_18 (and_18_out, q3, q1);
  and and_19 (and_19_out, Nq1, q2, Nq3);
  and and_20 (and_20_out, Nq1, q2, q3);
  and and_21 (L6, Nq1, q2, Nq3);
  and and_22 (L7, Nq1, q2, q3);
  and and_23 (L8, Nq1, Nq2, q3);
  or or_4 (L1, Nq1, and_13_out, and_14_out);
  or or_5 (L2, and_15_out, and_16_out);
  or or_6 (L3, and_17_out, and_18_out);
  or or_7 (L4, and_19_out, and_20_out);
  and and_24 (i1, Nx1, x2, q1, Nq2, Nq3);
  and and_25 (i2, x1, x2, q1, Nq2, q3);
  and and_26 (i3, Nx1, x2, q1, q2, Nq3);
  and and_27 (i4, Nx1, x2, Nq1, q2, Nq3);

  assign L5 = q1;
endmodule
