// Logisim project course.circ as structural Verilog: 16 circuits, main circuit btn
module btn (
  input  a,
  input  b,
  input  c,
  input  d,
  output press_out,
  output x1,
  output x2
);

  or or_1 (press_out, a, b, c, d);
  or or_2 (x1, c, d);
  or or_3 (x2, b, d);
endmodule

module newQ (
  input  x1_in,
  input  x2_in,
  input  q1_in,
  input  q2_in,
  input  q3_in,
  input  q4_in,
  output q1_out,
  output q2_out,
  output q3_out,
  output q4_out
);

  wire and_1_out, and_2_out, and_3_out, and_4_out, and_5_out, and_6_out, and_7_out, and_8_out, and_9_out,
       and_10_out, and_11_out, and_12_out, and_13_out, and_14_out, and_15_out, and_16_out, and_17_out,
       and_18_out, and_19_out, and_20_out, and_21_out, and_22_out, and_23_out, and_24_out, and_25_out,
       and_26_out, and_27_out, and_28_out;

  and and_1 (and_1_out, q1_in, q4_in, ~x1_in, ~x2_in);  // AND_Gate
  and and_2 (and_2_out, q1_in, q3_in, ~x1_in, ~x2_in);  // AND_Gate
  and and_3 (and_3_out, q2_in, q3_in, q4_in, ~x2_in);  // AND_Gate
  or or_1 (q1_out, and_1_out, and_2_out, and_3_out, and_4_out, and_5_out, and_7_out, and_6_out);
  and and_4 (and_4_out, q2_in, q3_in, q4_in, x1_in);
  and and_5 (and_5_out, q2_in, q3_in, x1_in, ~x2_in);  // AND_Gate
  and and_6 (and_6_out, ~q1_in, ~q2_in, ~q3_in, ~q4_in, x1_in, ~x2_in);  // AND_Gate
  and and_7 (and_7_out, q1_in, ~q3_in, ~q4_in, ~x1_in, x2_in);  // AND_Gate
  and and_8 (and_8_out, q1_in, q4_in, x2_in);
  and and_9 (and_9_out, q1_in, ~q3_in, x1_in);  // AND_Gate
  or or_2 (q2_out, and_8_out, and_9_out, and_10_out, and_11_out, and_12_out, and_13_out, and_14_out);
  and and_10 (and_10_out, q2_in, ~q3_in, ~x2_in);  // AND_Gate
  and and_11 (and_11_out, q1_in, ~q3_in, ~q4_in, ~x2_in);  // AND_Gate
  and and_12 (and_12_out, q2_in, q3_in, ~x1_in, x2_in);  // AND_Gate
  and and_13 (and_13_out, q2_in, ~q4_in, ~x1_in, ~x2_in);  // AND_Gate
  and and_14 (and_14_out, ~q1_in, ~q2_in, ~q3_in, ~q4_in, x2_in);  // AND_Gate
  and and_15 (and_15_out, q1_in, q4_in, x2_in);
  and and_16 (and_16_out, ~q2_in, ~q3_in, x1_in);  // AND_Gate
  or or_3 (q3_out, and_15_out, and_16_out, and_17_out, and_18_out, and_19_out, and_20_out, and_21_out);
  and and_17 (and_17_out, q1_in, ~q3_in, ~q4_in, ~x2_in);  // AND_Gate
  and and_18 (and_18_out, q2_in, q3_in, ~x1_in, x2_in);  // AND_Gate
  and and_19 (and_19_out, q3_in, ~q4_in, ~x1_in, ~x2_in);  // AND_Gate
  and and_20 (and_20_out, ~q1_in, ~q2_in, q3_in, ~q4_in);  // AND_Gate
  and and_21 (and_21_out, ~q1_in, ~q2_in, ~q3_in, q4_in, ~x2_in);  // AND_Gate
  and and_22 (and_22_out, q1_in, q4_in, ~x1_in, ~x2_in);  // AND_Gate
  and and_23 (and_23_out, ~q1_in, q3_in, ~q4_in, ~x2_in);  // AND_Gate
  and and_24 (and_24_out, ~q1_in, ~q4_in, ~x1_in, ~x2_in);  // AND_Gate
  or or_4 (q4_out, and_22_out, and_23_out, and_24_out, and_25_out, and_26_out, and_27_out, and_28_out);
  and and_25 (and_25_out, q2_in, ~q3_in, q4_in, x1_in, ~x2_in);  // AND_Gate
  and and_26 (and_26_out, q2_in, q3_in, q4_in, ~x1_in, x2_in);  // AND_Gate
  and and_27 (and_27_out, ~q1_in, ~q2_in, q3_in, ~q4_in, x1_in);  // AND_Gate
  and and_28 (and_28_out, ~q1_in, ~q2_in, ~q3_in, q4_in, ~x1_in, x2_in);  // AND_Gate
endmodule

module blockL (
  input  q1,
  input  q2,
  input  q3,
  input  q4,
  output L1,
  output L2,
  output L3,
  output L4,
  output L5,
  output L6,
  output L7,
  output L8,
  output L9
);

  wire and_1_out, and_2_out, and_3_out, and_4_out, and_5_out, and_6_out, and_7_out, and_8_out, and_9_out,
       and_14_out, and_15_out;

  and and_1 (and_1_out, ~q1, ~q4);  // AND_Gate
  or or_1 (L1, and_1_out, and_2_out, and_3_out, and_4_out);
  and and_2 (and_2_out, ~q1, q2, ~q3);  // AND_Gate
  and and_3 (and_3_out, ~q2, ~q3, ~q4);  // AND_Gate
  and and_4 (and_4_out, ~q1, ~q2, q3);  // AND_Gate
  and and_5 (and_5_out, ~q1, ~q3);  // AND_Gate
  and and_6 (and_6_out, ~q1, q2);  // AND_Gate
  or or_2 (L2, and_5_out, and_6_out, and_7_out, and_8_out, and_9_out);
  and and_7 (and_7_out, ~q1, q4);  // AND_Gate
  and and_8 (and_8_out, ~q2, ~q3, q4);  // AND_Gate
  and and_9 (and_9_out, q1, ~q2, q3, ~q4);  // AND_Gate
  and and_10 (L3, ~q1, ~q2);  // AND_Gate
  and and_11 (L4, ~q1, q2, ~q3);  // AND_Gate
  and and_12 (L5, ~q1, q2, ~q3, ~q4);  // AND_Gate
  and and_13 (L6, ~q1, q2, ~q3, q4);  // AND_Gate
  or or_3 (L7, and_14_out, and_15_out);
  and and_14 (and_14_out, ~q1, q2, q3);  // AND_Gate
  and and_15 (and_15_out, q1, ~q2, ~q3, ~q4);  // AND_Gate
  and and_16 (L8, q1, ~q2, ~q3, q4);  // AND_Gate
  and and_17 (L9, q1, ~q2, q3, ~q4);  // AND_Gate
endmodule

module blockI (
  input  press_in,
  input  q1,
  input  q2,
  input  q3,
  input  q4,
  input  x1,
  input  x2,
  output i1,
  output i2,
  output i3,
  output i4,
  output i5,
  output i6,
  output i7,
  output i8,
  output i9
);

  wire and_2_out, and_4_out, and_5_out, and_7_out, and_8_out, and_10_out, and_11_out, and_13_out, and_15_out,
       and_17_out, and_19_out, and_21_out, buffer_1_out, or_1_out, or_2_out;

  buf buffer_1 (buffer_1_out, press_in);
  and and_1 (i1, buffer_1_out, and_2_out);
  and and_2 (and_2_out, ~q1, ~q2, ~q3, q4, ~x1, x2);  // AND_Gate
  and and_3 (i2, buffer_1_out, and_4_out);
  and and_4 (and_4_out, ~q1, ~q2, q3, ~q4, ~x1, x2);  // AND_Gate
  and and_5 (and_5_out, ~q1, ~q2, q3, ~x2);  // AND_Gate
  and and_6 (i3, buffer_1_out, or_1_out);
  or or_1 (or_1_out, and_5_out, and_7_out, and_8_out);
  and and_7 (and_7_out, ~q1, ~q2, q3, q4);  // AND_Gate
  and and_8 (and_8_out, ~q1, ~q2, q3, x1);  // AND_Gate
  and and_9 (i4, buffer_1_out, or_2_out);
  or or_2 (or_2_out, and_10_out, and_11_out);
  and and_10 (and_10_out, ~q1, q2, ~q3, x1, ~x2);  // AND_Gate
  and and_11 (and_11_out, ~q1, ~q2, ~q3, ~q4, ~x1, x2);  // AND_Gate
  and and_12 (i5, buffer_1_out, and_13_out);
  and and_13 (and_13_out, ~q1, q2, q3, q4, ~x1, x2);  // AND_Gate
  and and_14 (i6, buffer_1_out, and_15_out);
  and and_15 (and_15_out, q1, ~q2, ~q3, ~q4, ~x1, x2);  // AND_Gate
  and and_16 (i7, buffer_1_out, and_17_out);
  and and_17 (and_17_out, ~q1, q2, q3, ~q4, ~x1, x2);  // AND_Gate
  and and_18 (i8, buffer_1_out, and_19_out);
  and and_19 (and_19_out, q1, ~q2, ~q3, q4, ~x1, ~x2);  // AND_Gate
  and and_20 (i9, buffer_1_out, and_21_out);
  and and_21 (and_21_out, q1, ~q2, q3, ~q4, ~x1, ~x2);  // AND_Gate
endmodule

module cstate (
  input  press_in,
  input  q1_in,
  input  q2_in,
  input  q3_in,
  input  q4_in,
  output q1_out,
  output q2_out,
  output q3_out,
  output q4_out
);

  D_Flip_Flop #(.trigger("falling")) d_ff_1 (.D(q1_in), .clk(press_in), .Q(q1_out));  // open: Qn, preset, reset
  D_Flip_Flop #(.trigger("falling")) d_ff_2 (.D(q2_in), .clk(press_in), .Q(q2_out));  // open: Qn, preset, reset
  D_Flip_Flop #(.trigger("falling")) d_ff_3 (.D(q3_in), .clk(press_in), .Q(q3_out));  // open: Qn, preset, reset
  D_Flip_Flop #(.trigger("falling")) d_ff_4 (.D(q4_in), .clk(press_in), .Q(q4_out));  // open: Qn, preset, reset
endmodule

module control (
  input  a,
  input  b,
  input  c,
  input  d,
  output i1,
  output i2,
  output i3,
  output i4,
  output i5,
  output i6,
  output i7,
  output i8,
  output i9,
  output L1,
  output L2,
  output L3,
  output L4,
  output L5,
  output L6,
  output L7,
  output L8,
  output L9
);

  wire btn_1_press_out, btn_1_x1, btn_1_x2, cstate_1_q1_out, cstate_1_q2_out, cstate_1_q3_out,
       cstate_1_q4_out, newq_1_q1_out, newq_1_q2_out, newq_1_q3_out, newq_1_q4_out;

  btn btn_1 (.a(a), .b(b), .c(c), .d(d), .press_out(btn_1_press_out), .x1(btn_1_x1), .x2(btn_1_x2));
  newQ newq_1 (
    .x1_in(btn_1_x1), .x2_in(btn_1_x2), .q1_in(cstate_1_q1_out), .q2_in(cstate_1_q2_out),
    .q3_in(cstate_1_q3_out), .q4_in(cstate_1_q4_out), .q1_out(newq_1_q1_out), .q2_out(newq_1_q2_out),
    .q3_out(newq_1_q3_out), .q4_out(newq_1_q4_out));
  cstate cstate_1 (
    .press_in(btn_1_press_out), .q1_in(newq_1_q1_out), .q2_in(newq_1_q2_out), .q3_in(newq_1_q3_out),
    .q4_in(newq_1_q4_out), .q1_out(cstate_1_q1_out), .q2_out(cstate_1_q2_out), .q3_out(cstate_1_q3_out),
    .q4_out(cstate_1_q4_out));
  blockI blocki_1 (
    .press_in(btn_1_press_out), .q1(cstate_1_q1_out), .q2(cstate_1_q2_out), .q3(cstate_1_q3_out),
    .q4(cstate_1_q4_out), .x1(btn_1_x1), .x2(btn_1_x2), .i1(i1), .i2(i2), .i3(i3), .i4(i4), .i5(i5), .i6(i6),
    .i7(i7), .i8(i8), .i9(i9));
  blockL blockl_1 (
    .q1(cstate_1_q1_out), .q2(cstate_1_q2_out), .q3(cstate_1_q3_out), .q4(cstate_1_q4_out), .L1(L1), .L2(L2),
    .L3(L3), .L4(L4), .L5(L5), .L6(L6), .L7(L7), .L8(L8), .L9(L9));
endmodule

module clocks (
  input  i1,
  input  i2,
  input  i3,
  input  CLK,
  output [15:0] digits
);

  wire and_1_out, controlled_buffer_1_out, counter_1_carry, counter_2_carry, d_ff_1_qn, xor_1_out, xor_2_out;
  wire [3:0] bit_extender_5_out, bit_extender_6_out;
  wire [7:0] counter_1_q, counter_2_q, counter_3_q, divider_1_out, divider_1_rem, divider_2_out,
       divider_2_rem, divider_3_out, divider_3_rem;

  D_Flip_Flop d_ff_1 (.clk(i3), .D(d_ff_1_qn), .Qn(d_ff_1_qn));  // open: Q, preset, reset
  Counter #(.max('h3b), .trigger("falling")) counter_1 (
    .Q(counter_1_q), .carry(counter_1_carry), .clk(xor_1_out));  // open: load, D, count, up, clr
  xor xor_1 (xor_1_out, i1, counter_2_carry);
  Counter #(.max('h3b), .trigger("falling")) counter_2 (
    .Q(counter_2_q), .carry(counter_2_carry), .clk(controlled_buffer_1_out));  // open: load, D, count, up, clr
  assign controlled_buffer_1_out = d_ff_1_qn ? CLK : 1'bz;  // Controlled_Buffer controlled_buffer_1
  Counter #(.max('h17), .trigger("falling")) counter_3 (
    .Q(counter_3_q), .clk(xor_2_out));  // open: load, D, count, carry, up, clr
  xor xor_2 (xor_2_out, i2, and_1_out);
  and and_1 (and_1_out, counter_1_carry, counter_2_carry);
  Divider divider_1 (.a(counter_3_q), .b(8'ha), .out(divider_1_out), .rem(divider_1_rem));  // open: upper
  Divider divider_2 (.a(counter_1_q), .b(8'ha), .out(divider_2_out), .rem(divider_2_rem));  // open: upper
  Divider divider_3 (.a(counter_2_q), .b(8'ha), .out(divider_3_out), .rem(divider_3_rem));  // open: upper
  Bit_Extender #(.out_width(4)) bit_extender_1 (.in(divider_1_out), .out(digits[15:12]));
  Bit_Extender #(.out_width(4)) bit_extender_2 (.in(divider_1_rem), .out(digits[11:8]));
  Bit_Extender #(.out_width(4)) bit_extender_3 (.in(divider_2_out), .out(digits[7:4]));
  Bit_Extender #(.out_width(4)) bit_extender_4 (.in(divider_2_rem), .out(digits[3:0]));
  Bit_Extender #(.out_width(4)) bit_extender_5 (.in(divider_3_out), .out(bit_extender_5_out));
  Bit_Extender #(.out_width(4)) bit_extender_6 (.in(divider_3_rem), .out(bit_extender_6_out));
  Hex_Digit_Display hex_digit_display_1 (.value(digits[15:12]));  // open: dp
  Hex_Digit_Display hex_digit_display_2 (.value(digits[11:8]));  // open: dp
  Hex_Digit_Display hex_digit_display_3 (.value(digits[7:4]));  // open: dp
  Hex_Digit_Display hex_digit_display_4 (.value(digits[3:0]));  // open: dp
  Hex_Digit_Display hex_digit_display_5 (.value(bit_extender_5_out));  // open: dp
  Hex_Digit_Display hex_digit_display_6 (.value(bit_extender_6_out));  // open: dp
endmodule

module iconv (
  input  [3:0] digit_in_binary,
  output [6:0] bits_indicator
);

  Multiplexer #(.select(4), .width(7)) multiplexer_1 (
    .in0(7'b0111111), .in1(7'b0001001), .in2(7'b1011110), .in3(7'b1011011), .in4(7'b1101001),
    .in5(7'b1110011), .in6(7'b1110111), .in7(7'b0011001), .in8({7{1'b1}}), .in9(7'b1111011),
    .out(bits_indicator), .sel(digit_in_binary));  // open: in10, in11, in12, in13, in14, in15
  _7_Segment_Display #(.decimalPoint("false")) u_7_segment_display_1 (
    .g(bits_indicator[6]), .f(bits_indicator[5]), .a(bits_indicator[4]), .b(bits_indicator[3]),
    .e(bits_indicator[2]), .d(bits_indicator[1]), .c(bits_indicator[0]));
endmodule

module iconvx4 (
  input  indicators,
  input  left_active,
  input  right_active,
  input  [15:0] digits,
  output [6:0] l1,
  output [6:0] l2,
  output [6:0] r1,
  output [6:0] r2
);

  wire and_1_out, and_2_out;
  wire [3:0] controlled_buffer_1_out, controlled_buffer_2_out, controlled_buffer_3_out,
       controlled_buffer_4_out;

  assign controlled_buffer_1_out = and_2_out ? digits[15:12] : 4'bz;  // Controlled_Buffer controlled_buffer_1
  assign controlled_buffer_2_out = and_2_out ? digits[11:8] : 4'bz;  // Controlled_Buffer controlled_buffer_2
  assign controlled_buffer_3_out = and_1_out ? digits[7:4] : 4'bz;  // Controlled_Buffer controlled_buffer_3
  and and_1 (and_1_out, right_active, indicators);
  and and_2 (and_2_out, left_active, indicators);
  assign controlled_buffer_4_out = and_1_out ? digits[3:0] : 4'bz;  // Controlled_Buffer controlled_buffer_4
  iconv iconv_1 (.digit_in_binary(controlled_buffer_1_out), .bits_indicator(l1));
  iconv iconv_2 (.digit_in_binary(controlled_buffer_2_out), .bits_indicator(l2));
  iconv iconv_3 (.digit_in_binary(controlled_buffer_3_out), .bits_indicator(r1));
  iconv iconv_4 (.digit_in_binary(controlled_buffer_4_out), .bits_indicator(r2));
endmodule

module sleep_mode (
  input  a_in,
  input  b_in,
  input  c_in,
  input  d_in,
  input  CLK,
  input  energy_eff_switcher,
  output indicators,
  output a_out,
  output b_out,
  output c_out,
  output d_out,
  output energy_eff_mode
);

  wire and_1_out, buffer_1_out, counter_1_carry, d_ff_1_qn, or_1_out, or_2_out;

  or or_1 (or_1_out, a_in, b_in, c_in, d_in);
  D_Flip_Flop d_ff_1 (
    .clk(energy_eff_switcher), .D(d_ff_1_qn), .Q(energy_eff_mode), .Qn(d_ff_1_qn));  // open: preset, reset
  and and_1 (and_1_out, ~or_1_out, buffer_1_out);  // AND_Gate
  buf buffer_1 (buffer_1_out, or_1_out);
  Counter #(.max('ha), .ongoal("stay"), .trigger("falling")) counter_1 (
    .carry(counter_1_carry), .clk(CLK), .clr(or_2_out));  // open: load, D, count, Q, up
  or or_2 (or_2_out, and_1_out, ~energy_eff_mode);  // OR_Gate
  not not_1 (indicators, counter_1_carry);
  and and_2 (a_out, a_in, indicators);
  and and_3 (b_out, b_in, indicators);
  and and_4 (c_out, c_in, indicators);
  and and_5 (d_out, d_in, indicators);
endmodule

module sec (
  input  clear,
  input  turn_off,
  input  turn_on,
  input  CLK,
  output [15:0] digits
);

  wire and_1_out, controlled_buffer_1_out, counter_1_carry, counter_2_carry, counter_3_carry;

  and and_1 (and_1_out, ~turn_off, turn_on);  // AND_Gate
  assign controlled_buffer_1_out = and_1_out ? CLK : 1'bz;  // Controlled_Buffer controlled_buffer_1
  Counter #(.max('h9), .trigger("falling"), .width(4)) counter_1 (
    .Q(digits[3:0]), .carry(counter_1_carry), .clk(controlled_buffer_1_out), .clr(clear));  // open: load, D, count, up
  Counter #(.max('h9), .trigger("falling"), .width(4)) counter_2 (
    .Q(digits[11:8]), .carry(counter_2_carry), .clk(counter_3_carry), .clr(clear));  // open: load, D, count, up
  Counter #(.max('h5), .trigger("falling"), .width(4)) counter_3 (
    .Q(digits[7:4]), .carry(counter_3_carry), .clk(counter_1_carry), .clr(clear));  // open: load, D, count, up
  Counter #(.max('h5), .trigger("falling"), .width(4)) counter_4 (
    .Q(digits[15:12]), .clk(counter_2_carry), .clr(clear));  // open: load, D, count, carry, up
endmodule

module budilnik (
  input  [15:0] time_clocks,
  input  plus_minute,
  input  plus_hour,
  input  on_off,
  input  CLK,
  output [15:0] digits,
  output work,
  output play
);

  wire and_1_out, comparator_1_eq, comparator_1_gt, comparator_1_lt, comparator_2_eq,
       controlled_buffer_1_out, counter_3_carry, d_ff_1_q, d_ff_1_qn, d_ff_2_qn, not_1_out, or_1_out;
  wire [3:0] counter_3_q;
  wire [7:0] counter_1_q, counter_2_q, divider_1_out, divider_1_rem, divider_2_out, divider_2_rem;

  Counter #(.max('h3b), .trigger("falling")) counter_1 (
    .Q(counter_1_q), .clk(plus_minute));  // open: load, D, count, carry, up, clr
  Divider divider_1 (.a(counter_1_q), .b(8'ha), .out(divider_1_out), .rem(divider_1_rem));  // open: upper
  Bit_Extender #(.out_width(4)) bit_extender_1 (.in(divider_1_out), .out(digits[7:4]));
  Bit_Extender #(.out_width(4)) bit_extender_2 (.in(divider_1_rem), .out(digits[3:0]));
  Counter #(.max('h17), .trigger("falling")) counter_2 (
    .Q(counter_2_q), .clk(plus_hour));  // open: load, D, count, carry, up, clr
  Divider divider_2 (.a(counter_2_q), .b(8'ha), .out(divider_2_out), .rem(divider_2_rem));  // open: upper
  Bit_Extender #(.out_width(4)) bit_extender_3 (.in(divider_2_out), .out(digits[15:12]));
  Bit_Extender #(.out_width(4)) bit_extender_4 (.in(divider_2_rem), .out(digits[11:8]));
  Comparator #(.width(16)) comparator_1 (
    .a(time_clocks), .b(digits), .gt(comparator_1_gt), .eq(comparator_1_eq), .lt(comparator_1_lt));
  or or_1 (or_1_out, comparator_1_gt, comparator_1_lt);
  assign controlled_buffer_1_out = and_1_out ? CLK : 1'bz;  // Controlled_Buffer controlled_buffer_1
  and and_1 (and_1_out, comparator_1_eq, ~d_ff_1_q);  // AND_Gate
  Counter #(.max('hc), .width(4)) counter_3 (
    .Q(counter_3_q), .carry(counter_3_carry), .clk(controlled_buffer_1_out), .clr(or_1_out));  // open: load, D, count, up
  not not_1 (not_1_out, comparator_2_eq);
  Comparator #(.width(4)) comparator_2 (.a(4'b0000), .b(counter_3_q), .eq(comparator_2_eq));  // open: gt, lt
  D_Flip_Flop #(.trigger("falling")) d_ff_1 (
    .clk(counter_3_carry), .D(d_ff_1_qn), .Q(d_ff_1_q), .Qn(d_ff_1_qn), .reset(or_1_out));  // open: preset
  and and_2 (play, not_1_out, work);
  D_Flip_Flop d_ff_2 (.clk(on_off), .D(d_ff_2_qn), .Q(work), .Qn(d_ff_2_qn));  // open: preset, reset
endmodule

module speaker (
  input  [6:0] volume_in,
  input  play_in,
  input  [55:0] sound,
  input  CLK,
  output [13:0] freq,
  output play_out,
  output [6:0] volume_out
);

  wire and_1_out, not_1_out;
  wire [1:0] counter_1_q;

  not not_1 (not_1_out, play_in);
  Counter #(.max('h3), .width(2)) counter_1 (
    .Q(counter_1_q), .clk(CLK), .clr(and_1_out));  // open: load, D, count, carry, up
  and and_1 (and_1_out, play_in, not_1_out);
  Multiplexer #(.select(2), .width(14)) multiplexer_1 (
    .in0(sound[13:0]), .in1(sound[27:14]), .in2(sound[41:28]), .in3(sound[55:42]), .out(freq),
    .sel(counter_1_q));

  assign play_out = play_in;
  assign volume_out = volume_in;
endmodule

module sound_choice (
  input  next_sound,
  output [55:0] sound,
  output [15:0] sound_number
);

  wire [2:0] counter_1_q;
  wire [15:0] bit_extender_1_out;

  Multiplexer #(.select(3), .width(56)) multiplexer_1 (
    .in0(56'h2000c003800c0), .in1(56'h1fc0ff07fc0ff), .in2(56'h4001800700140), .in3(56'h4001800500180),
    .in4(56'h40018007001e0), .in5(56'h4003000800000), .in6(56'h8000000800000), .in7(56'h7fc17f04fc17f),
    .out(sound), .sel(counter_1_q));
  Counter #(.max('h7), .width(3)) counter_1 (
    .Q(counter_1_q), .clk(next_sound));  // open: load, D, count, carry, up, clr
  assign bit_extender_1_out = {{13{1'b0}}, counter_1_q};  // Bit_Extender bit_extender_1
  Adder #(.width(16)) adder_1 (.a(bit_extender_1_out), .b(16'h1), .out(sound_number));  // open: cin, cout
endmodule

module main (
);

  wire a_out, b_out, budilnik_1_play, budilnik_1_work, c_out, clock_1_out, clock_2_out, clock_3_out,
       clock_4_out, clock_5_out, clock_6_out, clock_7_out, control_1_i4, control_1_i8, control_1_i9,
       control_1_l1, control_1_l2, control_1_l3, control_1_l4, control_1_l5, control_1_l6, control_1_l7,
       control_1_l8, control_1_l9, d_out, E_out, or_1_out, or_2_out, signalization_1_play,
       sleep_mode_1_energy_eff_mode, sleep_mode_1_indicators, speaker_1_play_out, speaker_2_play_out;
  wire [2:0] control_1_i1, control_1_i5, iconvx4_1_l1, iconvx4_1_l2, iconvx4_1_r1, iconvx4_1_r2;
  wire [3:0] iconvx4_1_l1_2, iconvx4_1_l2_2, iconvx4_1_r1_2, iconvx4_1_r2_2, sleep_mode_1_a_out;
  wire [6:0] slider_1_out, speaker_1_volume_out, speaker_2_volume_out;
  wire [13:0] speaker_1_freq, speaker_2_freq;
  wire [15:0] budilnik_1_digits, clocks_1_digits, controlled_buffer_1_out, sec_1_digits,
       sound_choice_1_sound_number, sound_choice_2_sound_number;
  wire [55:0] sound_choice_1_sound, sound_choice_2_sound;

  control control_1 (
    .a(sleep_mode_1_a_out[0]), .b(sleep_mode_1_a_out[1]), .c(sleep_mode_1_a_out[2]),
    .d(sleep_mode_1_a_out[3]), .i1(control_1_i1[0]), .i2(control_1_i1[1]), .i3(control_1_i1[2]),
    .i4(control_1_i4), .i5(control_1_i5[0]), .i6(control_1_i5[1]), .i7(control_1_i5[2]), .i8(control_1_i8),
    .i9(control_1_i9), .L1(control_1_l1), .L2(control_1_l2), .L3(control_1_l3), .L4(control_1_l4),
    .L5(control_1_l5), .L6(control_1_l6), .L7(control_1_l7), .L8(control_1_l8), .L9(control_1_l9));
  Clock clock_1 (.out(clock_1_out));
  Clock clock_2 (.out(clock_2_out));
  clocks clocks_1 (
    .i1(control_1_i1[0]), .i2(control_1_i1[1]), .i3(control_1_i1[2]), .CLK(clock_1_out),
    .digits(clocks_1_digits));
  sec sec_1 (
    .clear(control_1_i4), .turn_off(control_1_l5), .turn_on(control_1_l6), .CLK(clock_2_out),
    .digits(sec_1_digits));
  Clock clock_3 (.out(clock_3_out));
  Clock clock_4 (.out(clock_4_out));
  budilnik budilnik_1 (
    .time_clocks(clocks_1_digits), .plus_minute(control_1_i5[0]), .plus_hour(control_1_i5[1]),
    .on_off(control_1_i5[2]), .CLK(clock_3_out), .digits(budilnik_1_digits), .work(budilnik_1_work),
    .play(budilnik_1_play));
  sound_choice sound_choice_1 (
    .next_sound(control_1_i8), .sound(sound_choice_1_sound), .sound_number(sound_choice_1_sound_number));
  signalization signalization_1 (.time_clock(clocks_1_digits), .CLK(clock_4_out), .play(signalization_1_play));
  sound_choice sound_choice_2 (
    .next_sound(control_1_i9), .sound(sound_choice_2_sound), .sound_number(sound_choice_2_sound_number));
  or or_1 (or_1_out, control_1_l8, budilnik_1_play);
  Clock clock_5 (.out(clock_5_out));
  or or_2 (or_2_out, control_1_l9, signalization_1_play);
  Clock clock_6 (.out(clock_6_out));
  speaker speaker_1 (
    .volume_in(slider_1_out), .play_in(or_1_out), .sound(sound_choice_1_sound), .CLK(clock_5_out),
    .freq(speaker_1_freq), .play_out(speaker_1_play_out), .volume_out(speaker_1_volume_out));
  speaker speaker_2 (
    .volume_in(slider_1_out), .play_in(or_2_out), .sound(sound_choice_2_sound), .CLK(clock_6_out),
    .freq(speaker_2_freq), .play_out(speaker_2_play_out), .volume_out(speaker_2_volume_out));
  // Buzzer buzzer_1: pin names not known; wires that end beside it: speaker_1_freq, speaker_1_play_out, speaker_1_volume_out
  // Buzzer buzzer_2: pin names not known; wires that end beside it: speaker_2_freq, speaker_2_play_out, speaker_2_volume_out
  assign controlled_buffer_1_out = control_1_l9 ? sound_choice_2_sound_number : 16'bz;  // Controlled_Buffer controlled_buffer_1
  Button E (.out(E_out));
  assign controlled_buffer_1_out = control_1_l3 ? clocks_1_digits : 16'bz;  // Controlled_Buffer controlled_buffer_2
  assign controlled_buffer_1_out = control_1_l7 ? budilnik_1_digits : 16'bz;  // Controlled_Buffer controlled_buffer_3
  assign controlled_buffer_1_out = control_1_l8 ? sound_choice_1_sound_number : 16'bz;  // Controlled_Buffer controlled_buffer_4
  assign controlled_buffer_1_out = control_1_l4 ? sec_1_digits : 16'bz;  // Controlled_Buffer controlled_buffer_5
  Button a (.out(a_out));
  Button b (.out(b_out));
  Button c (.out(c_out));
  Button d (.out(d_out));
  Clock clock_7 (.out(clock_7_out));
  sleep_mode sleep_mode_1 (
    .a_in(a_out), .b_in(b_out), .c_in(c_out), .d_in(d_out), .CLK(clock_7_out), .energy_eff_switcher(E_out),
    .indicators(sleep_mode_1_indicators), .a_out(sleep_mode_1_a_out[0]), .b_out(sleep_mode_1_a_out[1]),
    .c_out(sleep_mode_1_a_out[2]), .d_out(sleep_mode_1_a_out[3]),
    .energy_eff_mode(sleep_mode_1_energy_eff_mode));
  iconvx4 iconvx4_1 (
    .indicators(sleep_mode_1_indicators), .left_active(control_1_l1), .right_active(control_1_l2),
    .digits(controlled_buffer_1_out), .l1({iconvx4_1_l1_2, iconvx4_1_l1}),
    .l2({iconvx4_1_l2_2, iconvx4_1_l2}), .r1({iconvx4_1_r1_2, iconvx4_1_r1}),
    .r2({iconvx4_1_r2_2, iconvx4_1_r2}));
  _7_Segment_Display #(.decimalPoint("false")) u_7_segment_display_1 (
    .g(iconvx4_1_l1_2[3]), .f(iconvx4_1_l1_2[2]), .a(iconvx4_1_l1_2[1]), .b(iconvx4_1_l1_2[0]),
    .e(iconvx4_1_l1[2]), .d(iconvx4_1_l1[1]), .c(iconvx4_1_l1[0]));
  _7_Segment_Display #(.decimalPoint("false")) u_7_segment_display_2 (
    .g(iconvx4_1_l2_2[3]), .f(iconvx4_1_l2_2[2]), .a(iconvx4_1_l2_2[1]), .b(iconvx4_1_l2_2[0]),
    .e(iconvx4_1_l2[2]), .d(iconvx4_1_l2[1]), .c(iconvx4_1_l2[0]));
  _7_Segment_Display #(.decimalPoint("false")) u_7_segment_display_3 (
    .g(iconvx4_1_r1_2[3]), .f(iconvx4_1_r1_2[2]), .a(iconvx4_1_r1_2[1]), .b(iconvx4_1_r1_2[0]),
    .e(iconvx4_1_r1[2]), .d(iconvx4_1_r1[1]), .c(iconvx4_1_r1[0]));
  _7_Segment_Display #(.decimalPoint("false")) u_7_segment_display_4 (
    .g(iconvx4_1_r2_2[3]), .f(iconvx4_1_r2_2[2]), .a(iconvx4_1_r2_2[1]), .b(iconvx4_1_r2_2[0]),
    .e(iconvx4_1_r2[2]), .d(iconvx4_1_r2[1]), .c(iconvx4_1_r2[0]));
  Slider #(.width(7)) slider_1 (.out(slider_1_out));
  LED led_1 (.in(budilnik_1_work));
  LED led_2 (.in(budilnik_1_play));
  LED led_3 (.in(signalization_1_play));
  LED led_4 (.in(sleep_mode_1_energy_eff_mode));

  // Notes on the sheet:
  //   Состояние будильника
  //   Сигнал будильника
  //   Сигнал сигнализации
  //   Режим энергосбережения
endmodule

module signalization (
  input  [15:0] time_clock,
  input  CLK,
  output play
);

  wire and_1_out, comparator_1_eq, comparator_1_gt, comparator_1_lt, comparator_2_gt, comparator_2_lt,
       controlled_buffer_1_out, counter_1_carry, d_ff_1_q, d_ff_1_qn, not_1_out, or_1_out;
  wire [3:0] counter_1_q;

  Comparator comparator_1 (
    .a(time_clock[7:0]), .b({8{1'b0}}), .gt(comparator_1_gt), .eq(comparator_1_eq), .lt(comparator_1_lt));
  or or_1 (or_1_out, comparator_1_gt, comparator_1_lt);
  not not_1 (not_1_out, d_ff_1_q);
  D_Flip_Flop #(.trigger("falling")) d_ff_1 (
    .clk(counter_1_carry), .D(d_ff_1_qn), .Q(d_ff_1_q), .Qn(d_ff_1_qn), .reset(or_1_out));  // open: preset
  and and_1 (and_1_out, comparator_1_eq, not_1_out);
  Counter #(.max('hc), .width(4)) counter_1 (
    .Q(counter_1_q), .carry(counter_1_carry), .clk(controlled_buffer_1_out), .clr(or_1_out));  // open: load, D, count, up
  assign controlled_buffer_1_out = and_1_out ? CLK : 1'bz;  // Controlled_Buffer controlled_buffer_1
  Comparator #(.width(4)) comparator_2 (
    .a(counter_1_q), .b(4'b0000), .gt(comparator_2_gt), .lt(comparator_2_lt));  // open: eq
  or or_2 (play, comparator_2_gt, comparator_2_lt);
endmodule
